// Logisim project 8bit_74_series_computer.circ as structural Verilog: 13 circuits, main circuit main
module main (
  input  in_1,
  input  in_2
);

  wire A_IN, A_OUT, ACC_IN, ACC_OUT, ALU_A_IS_BUS, ALU_C_IN, ALU_CARRYBORROW_FLAG_CLOCKED,
       ALU_CARRYBORROW_FLAG_IMM, ALU_M, ALU_NEGATIVE_FLAG_CLOCKED, ALU_NEGATIVE_FLAG_IMM, ALU_OUT, ALU_S0,
       ALU_S1, ALU_S2, ALU_S3, ALU_STORE_FLAGS, ALU_STORE_RESULT, ALU_ZERO_FLAG_CLOCKED, ALU_ZERO_FLAG_IMM,
       B_IN, B_OUT, button_1_out, C_IN, C_OUT, CLOCK_HALT, CONTROL_CLOCK, CU_CARRYBORROW_MIRROR,
       CU_NEGATIVE_MIRROR, CU_STEP_RESET, CU_ZERO_MIRROR, DATA_CLOCK, IR_IN, MANUAL_CLOCK_PULSE, MAR_IN,
       PC_COUNT, PC_IN, PC_OUT, RAM_IN, RAM_OUT, RAM_PROG_MEM_SELECT, RESET, SP_IN, SP_OUT;
  wire [2:0] CU_INSTRUCTION_MIRROR, CU_MICROCODE_STEP;
  wire [7:0] _2_1_b_2, A, ACC, ALU_RESULT_CLOCKED, ALU_RESULT_IMM, B, BUS, C, IR, MAR, PC,
       pull_resistor_1_node, RAM, SP;

  Button button_1 (.out(button_1_out));
  Button button_2 (.out(RESET));
  xor xor_1 (MANUAL_CLOCK_PULSE, in_1, button_1_out);
  // Probe on ACC_IN
  // Probe on ACC_OUT
  // Probe on A_IN
  // Probe on A_OUT
  // Probe on B_IN
  // Probe on B_OUT
  // Probe on C_IN
  // Probe on C_OUT
  // Probe on ALU_STORE_RESULT
  // Probe on ALU_STORE_FLAGS
  // Probe on ALU_OUT
  // Probe on ALU_A_IS_BUS
  // Probe on ALU_S0
  // Probe on ALU_S1
  // Probe on ALU_S2
  // Probe on ALU_S3
  // Probe on ALU_M
  // Probe on ALU_C_IN
  // Probe on MAR_IN
  // Probe on RAM_IN
  // Probe on RAM_OUT
  // Probe on RAM_PROG_MEM_SELECT
  // Probe on SP_IN
  // Probe on SP_OUT
  // Probe on PC_IN
  // Probe on PC_OUT
  // Probe on PC_COUNT
  // Probe on IR_IN
  // Probe on CU_STEP_RESET
  // Probe on CLOCK_HALT
  // Probe on DATA_CLOCK
  // Probe on CONTROL_CLOCK
  // Probe on BUS
  // Probe on PC
  // Probe on IR
  // Probe on SP
  // Probe on ACC
  // Probe on A
  // Probe on B
  // Probe on C
  // Probe on MAR
  // Probe on RAM
  // Probe on BUS
  // Probe on BUS
  // Probe on PC
  // Probe on PC
  // Probe on IR
  // Probe on IR
  // Probe on SP
  // Probe on SP
  // Probe on ACC
  // Probe on ACC
  // Probe on A
  // Probe on A
  // Probe on B
  // Probe on B
  // Probe on C
  // Probe on C
  // Probe on MAR
  // Probe on MAR
  // Probe on RAM
  // Probe on RAM
  Pull_Resistor pull_resistor_1 (.node(pull_resistor_1_node));
  // Probe on CU_ZERO_MIRROR
  // Probe on CU_NEGATIVE_MIRROR
  // Probe on CU_CARRYBORROW_MIRROR
  // Probe on CU_ZERO_MIRROR
  register_bus_L u_ACC (
    .\input (pull_resistor_1_node), .buffered_output(pull_resistor_1_node), .content(ACC),
    .input_enable(ACC_IN), .clock(DATA_CLOCK), .output_enable(ACC_OUT));
  _2_to_1_IO_L _2_1 (.A(ACC), .B(pull_resistor_1_node), .A_B(ALU_A_IS_BUS), .B_2(_2_1_b_2));
  ALU ALU (
    .carry_in(ALU_C_IN), .M(ALU_M), .S0(ALU_S0), .S1(ALU_S1), .S2(ALU_S2), .S3(ALU_S3),
    .store_result(ALU_STORE_RESULT), .clock(DATA_CLOCK),
    .unclocked_carryborrow_out(ALU_CARRYBORROW_FLAG_IMM),
    .clocked_carryborrow_out(ALU_CARRYBORROW_FLAG_CLOCKED), .unclocked_A___B(ALU_ZERO_FLAG_IMM),
    .clocked_A___B(ALU_ZERO_FLAG_CLOCKED), .clocked_zero(ALU_ZERO_FLAG_CLOCKED),
    .unclocked_zero(ALU_ZERO_FLAG_IMM), .tristate_clocked_result(pull_resistor_1_node), .A(_2_1_b_2),
    .B(pull_resistor_1_node), .result_output_enable(ALU_OUT), .unclocked_result(ALU_RESULT_IMM),
    .clocked_result(ALU_RESULT_CLOCKED), .unclocked_negative(ALU_NEGATIVE_FLAG_IMM),
    .clocked_negative(ALU_NEGATIVE_FLAG_CLOCKED), .store_flags(ALU_STORE_FLAGS));
  register_bus_L u_A (
    .\input (pull_resistor_1_node), .buffered_output(pull_resistor_1_node), .content(A), .input_enable(A_IN),
    .clock(DATA_CLOCK), .output_enable(A_OUT));
  register_bus_L u_B (
    .\input (pull_resistor_1_node), .buffered_output(pull_resistor_1_node), .content(B), .input_enable(B_IN),
    .clock(DATA_CLOCK), .output_enable(B_OUT));
  register_bus_L u_C (
    .\input (pull_resistor_1_node), .buffered_output(pull_resistor_1_node), .content(C), .input_enable(C_IN),
    .clock(DATA_CLOCK), .output_enable(C_OUT));
  register_bus_L u_SP (
    .\input (pull_resistor_1_node), .buffered_output(pull_resistor_1_node), .content(SP),
    .input_enable(SP_IN), .clock(DATA_CLOCK), .output_enable(SP_OUT));
  // Probe on ALU_RESULT_IMM
  // Probe on ALU_RESULT_CLOCKED
  // Probe on ALU_ZERO_FLAG_IMM
  // Probe on ALU_NEGATIVE_FLAG_IMM
  // Probe on ALU_CARRYBORROW_FLAG_IMM
  // Probe on ALU_ZERO_FLAG_IMM
  // Probe on ALU_ZERO_FLAG_CLOCKED
  // Probe on ALU_NEGATIVE_FLAG_CLOCKED
  // Probe on ALU_CARRYBORROW_FLAG_CLOCKED
  // Probe on ALU_ZERO_FLAG_CLOCKED
  // Probe on CU_INSTRUCTION_MIRROR
  // Probe on CU_MICROCODE_STEP
  program_counter u_PC (
    .\input (pull_resistor_1_node), .count(PC_COUNT), .clock(DATA_CLOCK), .output_enable(PC_OUT),
    .tristate_output(pull_resistor_1_node), .in(PC_IN), .contents(PC), .reset(RESET));
  // Probe on CU_INSTRUCTION_MIRROR
  // Probe on CU_INSTRUCTION_MIRROR
  // Probe on CU_MICROCODE_STEP
  // Probe on CU_MICROCODE_STEP
  // Probe on ALU_RESULT_IMM
  // Probe on ALU_RESULT_IMM
  // Probe on ALU_RESULT_CLOCKED
  // Probe on ALU_RESULT_CLOCKED

  // Other names for the same wires on the sheet: MANUAL_AUTO_CLOCK_MODE = in_2
endmodule

module ALU (
  input  [7:0] A,
  input  [7:0] B,
  input  carry_in,
  input  M,
  input  S0,
  input  S1,
  input  S2,
  input  S3,
  input  result_output_enable,
  input  clock,
  input  store_result,
  input  store_flags,
  output unclocked_zero,
  output clocked_zero,
  output unclocked_negative,
  output clocked_negative,
  output unclocked_carryborrow_out,
  output clocked_carryborrow_out,
  output unclocked_A___B,
  output clocked_A___B,
  output [7:0] tristate_clocked_result,
  output [7:0] unclocked_result,
  output [7:0] clocked_result
);

  wire and_2_out, and_3_out, and_4_out, and_5_out, n74ls181_1_a_b, n74ls181_1_carry_out_bar, n74ls181_2_a_b,
       n74ls181_2_carry_out_bar, nor_1_out, nor_2_out, nor_3_out, nor_4_out, nor_5_out, nor_6_out, nor_7_out,
       nor_8_out, not_2_out, not_3_out, not_4_out, not_5_out, not_6_out;

  and and_1 (unclocked_A___B, n74ls181_1_a_b, n74ls181_2_a_b);
  not not_1 (unclocked_carryborrow_out, n74ls181_2_carry_out_bar);
  not not_2 (not_2_out, carry_in);
  _74LS181 u_74ls181_1 (
    .B(B[3:0]), .A(A[3:0]), .M(M), .carry_in_bar(not_2_out), .carry_out_bar(n74ls181_1_carry_out_bar),
    .F(unclocked_result[3:0]), .A_B(n74ls181_1_a_b), .S0(S0), .S1(S1), .S2(S2), .S3(S3));  // open: Y, X
  _74LS181 u_74ls181_2 (
    .B(B[7:4]), .A(A[7:4]), .M(M), .carry_in_bar(n74ls181_1_carry_out_bar),
    .carry_out_bar(n74ls181_2_carry_out_bar), .F({unclocked_negative, unclocked_result[6:4]}),
    .A_B(n74ls181_2_a_b), .S0(S0), .S1(S1), .S2(S2), .S3(S3));  // open: Y, X
  not not_3 (not_3_out, store_result);
  not not_4 (not_4_out, clock);
  not not_5 (not_5_out, store_flags);
  not not_6 (not_6_out, clock);
  nor nor_1 (nor_1_out, unclocked_result[0], unclocked_result[1]);
  nor nor_2 (nor_2_out, unclocked_result[2], unclocked_result[3]);
  nor nor_3 (nor_3_out, unclocked_result[4], unclocked_result[5]);
  nor nor_4 (nor_4_out, unclocked_result[6], unclocked_negative);
  nor nor_5 (nor_5_out, not_3_out, nor_6_out);
  nor nor_6 (nor_6_out, nor_5_out, not_4_out);
  nor nor_7 (nor_7_out, not_5_out, nor_8_out);
  nor nor_8 (nor_8_out, nor_7_out, not_6_out);
  and and_2 (and_2_out, nor_1_out, nor_2_out);
  and and_3 (and_3_out, nor_3_out, nor_4_out);
  and and_4 (and_4_out, nor_5_out, clock);
  and and_5 (and_5_out, nor_7_out, clock);
  and and_6 (unclocked_zero, and_2_out, and_3_out);
  Register result (
    .D({unclocked_negative, unclocked_result[6:0]}), .en(1'b1), .Q(clocked_result), .clk(and_4_out),
    .clr(1'b0));
  assign tristate_clocked_result = result_output_enable ? clocked_result : 8'bz;  // Controlled_Buffer controlled_buffer_1
  Register #(.width(4)) register_1 (
    .D({unclocked_A___B, unclocked_carryborrow_out, unclocked_negative, unclocked_zero}), .en(1'b1),
    .Q({clocked_A___B, clocked_carryborrow_out, clocked_negative, clocked_zero}), .clk(and_5_out), .clr(1'b0));

  assign unclocked_result[7] = unclocked_negative;
endmodule

module register_bus_R (
  input  [7:0] \input ,
  input  input_enable,
  input  clock,
  input  output_enable,
  output [7:0] content,
  output [7:0] buffered_output
);

  wire and_1_out;

  Register register_1 (.D(\input ), .en(1'b1), .Q(content), .clk(and_1_out), .clr(1'b0));
  and and_1 (and_1_out, input_enable, clock);
  assign buffered_output = output_enable ? content : 8'bz;  // Controlled_Buffer controlled_buffer_1
endmodule

module register_bus_L (
  input  [7:0] \input ,
  input  input_enable,
  input  clock,
  input  output_enable,
  output [7:0] content,
  output [7:0] buffered_output
);

  wire and_1_out;

  Register register_1 (.D(\input ), .en(1'b1), .Q(content), .clk(and_1_out), .clr(1'b0));
  and and_1 (and_1_out, input_enable, clock);
  assign buffered_output = output_enable ? content : 8'bz;  // Controlled_Buffer controlled_buffer_1
endmodule

module clock (
  input  Halt,
  input  Auto_Manual,
  input  Reset,
  input  Manual_clock,
  output Clock,
  output Control_Clock
);

  wire Auto_clock_out, nand_1_out, nand_2_out, nand_3_out, nand_4_out, nand_5_out, nand_6_out, nand_7_out,
       nor_1_out, nor_2_out, nor_3_out, nor_4_out, not_1_out, not_2_out;

  Clock #(.highDuration(4), .lowDuration(4)) Auto_clock (.out(Auto_clock_out));
  nand nand_1 (nand_1_out, Auto_Manual, Auto_Manual);
  nand nand_2 (nand_2_out, Auto_Manual, Manual_clock);
  nand nand_3 (nand_3_out, nand_1_out, Auto_clock_out);
  nand nand_4 (nand_4_out, nand_2_out, nand_3_out);
  nor nor_1 (nor_1_out, nand_4_out, nand_4_out);
  nor nor_2 (nor_2_out, Halt, Reset);
  nor nor_3 (nor_3_out, Reset, nor_4_out);
  nor nor_4 (nor_4_out, nor_3_out, nor_1_out);
  nand nand_5 (nand_5_out, nor_3_out, nand_4_out);
  nand nand_6 (nand_6_out, nand_5_out, nand_5_out);
  nand nand_7 (nand_7_out, nand_6_out, nand_6_out);
  J_K_Flip_Flop j_k_ff_1 (
    .J(1'b1), .clk(nand_6_out), .K(1'b1), .Q(Clock), .preset(1'b0), .en(1'b1), .reset(not_1_out));  // open: Qn
  not not_1 (not_1_out, nor_2_out);
  J_K_Flip_Flop j_k_ff_2 (
    .J(1'b1), .clk(nand_7_out), .K(1'b1), .Q(Control_Clock), .preset(1'b0), .en(1'b1), .reset(not_2_out));  // open: Qn
  not not_2 (not_2_out, nor_2_out);
endmodule

module RAM (
  input  [7:0] \input ,
  input  input_enable,
  input  [7:0] address,
  input  Select_prog_mem,
  input  clock,
  input  output_enable,
  output [7:0] current_data,
  output [7:0] tristate_output
);

  wire not_1_out;

  RAM_part #(.addrWidth(9)) ram_1 (
    .addr({Select_prog_mem, address}), .data(current_data), .sel(1'b1), .clk(clock), .ld(not_1_out),
    .clr(1'b0));
  not not_1 (not_1_out, input_enable);
  assign current_data = input_enable ? \input  : 8'bz;  // Controlled_Buffer controlled_buffer_1
  assign tristate_output = output_enable ? current_data : 8'bz;  // Controlled_Buffer controlled_buffer_2
endmodule

module program_counter (
  input  in,
  input  output_enable,
  input  [7:0] \input ,
  input  count,
  input  clock,
  input  reset,
  output [7:0] tristate_output,
  output [7:0] contents
);

  Counter counter_1 (.load(in), .D(\input ), .count(count), .Q(contents), .clk(clock), .clr(reset));  // open: carry
  assign tristate_output = output_enable ? contents : 8'bz;  // Controlled_Buffer controlled_buffer_1
endmodule

module control_unit (
  input  [7:0] instruction,
  input  zero_flag,
  input  negative_flag,
  input  carryborrow_flag,
  input  equal_flag,
  input  control_clock,
  input  clear,
  input  sim_only_clear,
  output ACC_IN,
  output ACC_OUT,
  output A_IN,
  output [7:0] mirror_instruction,
  output A_OUT,
  output B_IN,
  output B_OUT,
  output C_IN,
  output C_OUT,
  output ALU_STORE_RESULT,
  output ALU_STORE_FLAGS,
  output ALU_OUT,
  output mirror_zero_flag,
  output ALU_A_IS_BUS,
  output mirror_negative_flag,
  output ALU_S0,
  output mirror_carryborrow_flag,
  output ALU_S1,
  output mirror_equal_flag,
  output ALU_S2,
  output ALU_S3,
  output [2:0] microcode_step,
  output ALU_M,
  output ALU_C_IN,
  output MAR_IN,
  output RAM_IN,
  output RAM_OUT,
  output RAM_SEL_PROG_MEM,
  output SP_IN,
  output SP_OUT,
  output PC_IN,
  output PC_OUT,
  output PC_COUNT,
  output IR_IN,
  output CU_STEP_RESET,
  output CLOCK_HALT
);

  wire not_1_out;
  wire [7:6] rom_4_data;

  not not_1 (not_1_out, CU_STEP_RESET);
  Register u_mirror_instruction (
    .D(instruction), .en(1'b1), .Q(mirror_instruction), .clk(control_clock), .clr(sim_only_clear));
  Register #(.width(4)) mirror_flags (
    .D({equal_flag, carryborrow_flag, negative_flag, zero_flag}), .en(1'b1),
    .Q({mirror_equal_flag, mirror_carryborrow_flag, mirror_negative_flag, mirror_zero_flag}),
    .clk(control_clock), .clr(sim_only_clear));
  Counter #(.width(3), .max('h7)) microcode_step_counter (
    .load(CU_STEP_RESET), .D(3'b000), .count(not_1_out), .Q(microcode_step), .clk(control_clock), .clr(clear));  // open: carry
  ROM #(.addrWidth(15)) rom_1 (
    .addr({microcode_step, mirror_equal_flag, mirror_carryborrow_flag, mirror_negative_flag, mirror_zero_flag, mirror_instruction}),
    .data({C_OUT, C_IN, B_OUT, B_IN, A_OUT, A_IN, ACC_OUT, ACC_IN}), .sel(1'b1));
  ROM #(.addrWidth(15)) rom_2 (
    .addr({microcode_step, mirror_equal_flag, mirror_carryborrow_flag, mirror_negative_flag, mirror_zero_flag, mirror_instruction}),
    .data({ALU_S3, ALU_S2, ALU_S1, ALU_S0, ALU_A_IS_BUS, ALU_OUT, ALU_STORE_FLAGS, ALU_STORE_RESULT}),
    .sel(1'b1));
  ROM #(.addrWidth(15)) rom_3 (
    .addr({microcode_step, mirror_equal_flag, mirror_carryborrow_flag, mirror_negative_flag, mirror_zero_flag, mirror_instruction}),
    .data({SP_OUT, SP_IN, RAM_SEL_PROG_MEM, RAM_OUT, RAM_IN, MAR_IN, ALU_C_IN, ALU_M}), .sel(1'b1));
  ROM #(.addrWidth(15)) rom_4 (
    .addr({microcode_step, mirror_equal_flag, mirror_carryborrow_flag, mirror_negative_flag, mirror_zero_flag, mirror_instruction}),
    .data({rom_4_data, CLOCK_HALT, CU_STEP_RESET, IR_IN, PC_COUNT, PC_OUT, PC_IN}), .sel(1'b1));

  // Notes on the sheet:
  //   microcode 3
  //   microcode 2
  //   microcode 1
  //   microcode 0
  //   contents of rom_1 (hex, n*v repeats v):
  //   4*10 4*c 4*10 4*8 4*0 4*2 72*0 4*10 4*c 4*0 4*2 16*0 4*10 4*c 4*0 4*2 80*0 4*10 4*c 4*10 4*8 4*0 4*2
  //   200*0 4*10 4*c 8 10 8 10 2 20 2 20 0 2 0 2 108*0 4*10 4*c 4*2 20*0 4*10 4*c 4*1
  //   contents of rom_2 (hex, n*v repeats v):
  //   4*4 4*1 4*4 4*5 4*1 76*0 4*4 4*1 4*20 20*0 4*4 4*1 4*10 84*0 4*4 4*1 4*4 4*5 4*81 204*0 4*4 4*1 0 4
  //   0 4 0 1 0 1 112*0 4*4 4*1 24*0 4*4 4*1
  //   contents of rom_3 (hex, n*v repeats v):
  //   16*0 4*2 84*0 4*1 28*0 4*2
  //   contents of rom_4 (hex, n*v repeats v):
  //   16*0 4*2 84*0 4*1 28*0 4*2
endmodule

module _74LS181 (
  input  S0,
  input  S1,
  input  S2,
  input  S3,
  input  [3:0] B,
  input  [3:0] A,
  input  M,
  input  carry_in_bar,
  output Y,
  output carry_out_bar,
  output X,
  output [3:0] F,
  output A_B
);

  wire and_1_out, and_2_out, and_3_out, and_4_out, and_5_out, and_6_out, and_7_out, and_8_out, and_9_out,
       and_10_out, and_11_out, and_12_out, and_13_out, and_14_out, and_15_out, and_16_out, and_17_out,
       and_18_out, and_19_out, and_20_out, and_21_out, and_22_out, and_23_out, and_24_out, and_25_out,
       and_26_out, and_27_out, and_28_out, nand_1_out, nand_3_out, nor_1_out, nor_2_out, nor_3_out,
       nor_4_out, nor_5_out, nor_6_out, nor_7_out, nor_8_out, nor_10_out, nor_11_out, nor_12_out, not_1_out,
       not_2_out, not_3_out, not_4_out, not_5_out, xor_1_out, xor_2_out, xor_3_out, xor_4_out;

  not not_1 (not_1_out, B[3]);
  not not_2 (not_2_out, B[2]);
  not not_3 (not_3_out, B[1]);
  not not_4 (not_4_out, B[0]);
  not not_5 (not_5_out, M);
  and and_1 (and_1_out, B[3], S3, A[3]);
  and and_2 (and_2_out, A[3], S2, not_1_out);
  and and_3 (and_3_out, not_1_out, S1);
  and and_4 (and_4_out, S0, B[3]);
  and and_5 (and_5_out, B[2], S3, A[2]);
  and and_6 (and_6_out, A[2], S2, not_2_out);
  and and_7 (and_7_out, not_2_out, S1);
  and and_8 (and_8_out, S0, B[2]);
  and and_9 (and_9_out, B[1], S3, A[1]);
  and and_10 (and_10_out, A[1], S2, not_3_out);
  and and_11 (and_11_out, not_3_out, S1);
  and and_12 (and_12_out, S0, B[1]);
  and and_13 (and_13_out, B[0], S3, A[0]);
  and and_14 (and_14_out, A[0], S2, not_4_out);
  and and_15 (and_15_out, not_4_out, S1);
  and and_16 (and_16_out, S0, B[0]);
  nor nor_1 (nor_1_out, and_1_out, and_2_out);
  nor nor_2 (nor_2_out, and_3_out, and_4_out, A[3]);
  nor nor_3 (nor_3_out, and_5_out, and_6_out);
  nor nor_4 (nor_4_out, and_7_out, and_8_out, A[2]);
  nor nor_5 (nor_5_out, and_9_out, and_10_out);
  nor nor_6 (nor_6_out, and_11_out, and_12_out, A[1]);
  nor nor_7 (nor_7_out, and_13_out, and_14_out);
  nor nor_8 (nor_8_out, and_15_out, and_16_out, A[0]);
  xor xor_1 (xor_1_out, nor_1_out, nor_2_out);
  xor xor_2 (xor_2_out, nor_3_out, nor_4_out);
  xor xor_3 (xor_3_out, nor_5_out, nor_6_out);
  xor xor_4 (xor_4_out, nor_7_out, nor_8_out);
  and and_17 (and_17_out, nor_1_out, nor_4_out);
  and and_18 (and_18_out, nor_1_out, nor_3_out, nor_6_out);
  and and_19 (and_19_out, nor_1_out, nor_3_out, nor_5_out, nor_8_out);
  nand nand_1 (nand_1_out, nor_1_out, nor_3_out, nor_5_out, nor_7_out, carry_in_bar);
  nand nand_2 (X, nor_1_out, nor_3_out, nor_5_out, nor_7_out);
  and and_20 (and_20_out, carry_in_bar, nor_7_out, nor_5_out, nor_3_out, not_5_out);
  and and_21 (and_21_out, nor_5_out, nor_3_out, nor_8_out, not_5_out);
  and and_22 (and_22_out, nor_3_out, nor_6_out, not_5_out);
  and and_23 (and_23_out, nor_4_out, not_5_out);
  and and_24 (and_24_out, carry_in_bar, nor_7_out, nor_5_out, not_5_out);
  and and_25 (and_25_out, nor_5_out, nor_8_out, not_5_out);
  and and_26 (and_26_out, nor_6_out, not_5_out);
  and and_27 (and_27_out, carry_in_bar, nor_7_out, not_5_out);
  and and_28 (and_28_out, nor_8_out, not_5_out);
  nand nand_3 (nand_3_out, carry_in_bar, not_5_out);
  nor nor_9 (Y, nor_2_out, and_17_out, and_18_out, and_19_out);
  nor nor_10 (nor_10_out, and_20_out, and_21_out, and_22_out, and_23_out);
  nor nor_11 (nor_11_out, and_24_out, and_25_out, and_26_out);
  nor nor_12 (nor_12_out, and_27_out, and_28_out);
  or or_1 (carry_out_bar, ~Y, ~nand_1_out);  // OR_Gate
  xor xor_5 (F[3], xor_1_out, nor_10_out);
  xor xor_6 (F[2], xor_2_out, nor_11_out);
  xor xor_7 (F[1], xor_3_out, nor_12_out);
  xor xor_8 (F[0], xor_4_out, nand_3_out);
  and and_29 (A_B, F[3], F[2], F[1], F[0]);
endmodule

module test_74LS181 (
  input  [3:0] in_1,
  input  [3:0] in_2,
  input  in_3,
  input  in_4,
  input  in_5,
  input  in_6,
  input  in_7,
  input  in_8,
  input  [7:0] in_9,
  input  [7:0] in_10,
  input  in_11,
  input  in_12,
  input  in_13,
  input  in_14,
  input  in_15,
  input  in_16,
  output out_17,
  output out_18,
  output out_19,
  output out_20,
  output out_21,
  output out_22
);

  wire n74ls181_2_a_b, n74ls181_2_carry_out_bar, n74ls181_3_a_b;
  wire [3:0] n74ls181_1_f, n74ls181_2_f, n74ls181_3_f;

  and and_1 (out_21, n74ls181_2_a_b, n74ls181_3_a_b);
  _74LS181 u_74ls181_1 (
    .B(in_2), .A(in_1), .M(in_4), .carry_in_bar(in_3), .Y(out_18), .carry_out_bar(out_20), .X(out_19),
    .F(n74ls181_1_f), .A_B(out_17), .S0(in_5), .S1(in_6), .S2(in_7), .S3(in_8));
  _74LS181 u_74ls181_2 (
    .B(in_10[3:0]), .A(in_9[3:0]), .M(in_12), .carry_in_bar(in_11), .carry_out_bar(n74ls181_2_carry_out_bar),
    .F(n74ls181_2_f), .A_B(n74ls181_2_a_b), .S0(in_13), .S1(in_14), .S2(in_15), .S3(in_16));  // open: Y, X
  _74LS181 u_74ls181_3 (
    .B(in_10[7:4]), .A(in_9[7:4]), .M(in_12), .carry_in_bar(n74ls181_2_carry_out_bar),
    .carry_out_bar(out_22), .F(n74ls181_3_f), .A_B(n74ls181_3_a_b), .S0(in_13), .S1(in_14), .S2(in_15),
    .S3(in_16));  // open: Y, X
  // Probe on in_1
  // Probe on in_1
  // Probe on in_1
  // Probe on in_2
  // Probe on in_2
  // Probe on in_2
  // Probe on n74ls181_1_f
  // Probe on n74ls181_1_f
  // Probe on n74ls181_1_f
  // Probe on in_9
  // Probe on in_9
  // Probe on in_9
  // Probe on in_10
  // Probe on in_10
  // Probe on in_10
  // Probe on {n74ls181_3_f, n74ls181_2_f}
  // Probe on {n74ls181_3_f, n74ls181_2_f}
  // Probe on {n74ls181_3_f, n74ls181_2_f}
endmodule

module test (
  input  in_1,
  input  in_2,
  input  in_3,
  input  in_4,
  input  [7:0] in_5,
  input  in_6,
  input  [7:0] in_7,
  input  in_8,
  input  in_9,
  input  in_10,
  input  in_11,
  input  in_12,
  input  in_13
);

  wire [7:0] n2_to_1_io_r_1_b_2, program_counter_1_contents, program_counter_2_contents, pull_resistor_1_node;

  _2_to_1_IO_R u_2_to_1_io_r_1 (.A(in_5), .B(in_7), .A_B(in_4), .B_2(n2_to_1_io_r_1_b_2));
  // Probe on n2_to_1_io_r_1_b_2
  // Probe on pull_resistor_1_node
  Pull_Resistor pull_resistor_1 (.node(pull_resistor_1_node));
  program_counter program_counter_1 (
    .\input (pull_resistor_1_node), .count(in_3), .clock(in_6), .output_enable(in_2),
    .tristate_output(pull_resistor_1_node), .in(in_1), .contents(program_counter_1_contents), .reset(in_8));
  program_counter program_counter_2 (
    .\input (pull_resistor_1_node), .count(in_11), .clock(in_12), .output_enable(in_10),
    .tristate_output(pull_resistor_1_node), .in(in_9), .contents(program_counter_2_contents), .reset(in_13));
  // Probe on program_counter_1_contents
  // Probe on program_counter_2_contents
endmodule

module _2_to_1_IO_R (
  input  [7:0] A,
  input  [7:0] B,
  input  A_B,
  output [7:0] B_2
);

  Multiplexer #(.width(8)) multiplexer_1 (.in0(A), .in1(B), .out(B_2), .sel(A_B), .en(1'b1));
endmodule

module _2_to_1_IO_L (
  input  [7:0] A,
  input  [7:0] B,
  input  A_B,
  output [7:0] B_2
);

  Multiplexer #(.width(8)) multiplexer_1 (.in0(A), .in1(B), .out(B_2), .sel(A_B), .en(1'b1));
endmodule
