// Logisim project sixteen-bit-computer.circ as structural Verilog: 17 circuits, main circuit main
module main (
  input  in_1,
  input  in_2,
  input  in_3,
  input  in_4,
  input  in_5,
  input  in_6,
  output out_7,
  output out_8,
  output out_9,
  output [15:0] out_10,
  output out_11,
  output out_12,
  output [15:0] out_13,
  output out_14,
  output out_15,
  output out_16,
  output [15:0] out_17,
  output out_18,
  output out_19,
  output [15:0] out_20,
  output out_21,
  output out_22,
  output out_23,
  output out_24,
  output out_25,
  output [15:0] out_26,
  output out_27,
  output out_28,
  output out_29,
  output out_30,
  output out_31,
  output out_32,
  output out_33,
  output out_34,
  output out_35,
  output [15:0] out_36,
  output out_37,
  output out_38,
  output out_39,
  output out_40,
  output out_41,
  output out_42,
  output out_43,
  output out_44,
  output [15:0] out_45,
  output out_46,
  output out_47,
  output out_48,
  output out_49,
  output [15:0] out_50,
  output out_51,
  output [15:0] out_52,
  output [2:0] out_53,
  output [15:0] out_54,
  output out_55,
  output [15:0] out_56,
  output out_57,
  output out_58,
  output out_59,
  output [15:0] out_60,
  output out_61,
  output out_62
);

  wire AUTO_CLOCK, button_2_out, button_3_out, cpu_1_out_13, cpu_1_out_17, cpu_1_out_64, MANUAL_CLOCK,
       multiplexer_1_out, RESET, SIM_ONLY_RESET;
  wire [15:0] DATA;

  Button button_1 (.out(SIM_ONLY_RESET));
  Button button_2 (.out(button_2_out));
  Button button_3 (.out(button_3_out));
  Clock_part clock_1 (.out(AUTO_CLOCK));
  LED led_1 (.in(out_7));
  LED led_2 (.in(out_9));
  LED led_3 (.in(out_11));
  LED led_4 (.in(out_14));
  LED led_5 (.in(out_16));
  LED led_6 (.in(out_18));
  LED led_7 (.in(out_21));
  LED led_8 (.in(out_23));
  LED led_9 (.in(out_28));
  LED led_10 (.in(out_31));
  LED led_11 (.in(out_33));
  LED led_12 (.in(out_37));
  LED led_13 (.in(out_39));
  LED led_14 (.in(out_42));
  LED led_15 (.in(out_44));
  LED led_16 (.in(out_47));
  LED led_17 (.in(out_48));
  LED led_18 (.in(out_51));
  xor xor_1 (RESET, button_2_out, in_1);
  xor xor_2 (MANUAL_CLOCK, in_4, button_3_out);
  LED led_19 (.in(out_8));
  LED led_20 (.in(out_12));
  LED led_21 (.in(out_15));
  LED led_22 (.in(out_19));
  LED led_23 (.in(out_24));
  LED led_24 (.in(out_29));
  LED led_25 (.in(out_32));
  LED led_26 (.in(out_35));
  LED led_27 (.in(out_41));
  LED led_28 (.in(out_46));
  LED led_29 (.in(out_49));
  Multiplexer #(.enable("false")) multiplexer_1 (
    .in0(MANUAL_CLOCK), .in1(AUTO_CLOCK), .out(multiplexer_1_out), .sel(in_3));
  DotMatrix #(.matrixcols(16), .matrixrows(1)) dotmatrix_1 (
    .col0(out_13[15]), .col1(out_13[14]), .col2(out_13[13]), .col3(out_13[12]), .col4(out_13[11]),
    .col5(out_13[10]), .col6(out_13[9]), .col7(out_13[8]), .col8(out_13[7]), .col9(out_13[6]),
    .col10(out_13[5]), .col11(out_13[4]), .col12(out_13[3]), .col13(out_13[2]), .col14(out_13[1]),
    .col15(out_13[0]));
  DotMatrix #(.matrixcols(16), .matrixrows(1)) dotmatrix_2 (
    .col0(out_20[15]), .col1(out_20[14]), .col2(out_20[13]), .col3(out_20[12]), .col4(out_20[11]),
    .col5(out_20[10]), .col6(out_20[9]), .col7(out_20[8]), .col8(out_20[7]), .col9(out_20[6]),
    .col10(out_20[5]), .col11(out_20[4]), .col12(out_20[3]), .col13(out_20[2]), .col14(out_20[1]),
    .col15(out_20[0]));
  DotMatrix #(.matrixcols(16), .matrixrows(1)) dotmatrix_3 (
    .col0(out_26[15]), .col1(out_26[14]), .col2(out_26[13]), .col3(out_26[12]), .col4(out_26[11]),
    .col5(out_26[10]), .col6(out_26[9]), .col7(out_26[8]), .col8(out_26[7]), .col9(out_26[6]),
    .col10(out_26[5]), .col11(out_26[4]), .col12(out_26[3]), .col13(out_26[2]), .col14(out_26[1]),
    .col15(out_26[0]));
  DotMatrix #(.matrixcols(16), .matrixrows(1)) dotmatrix_4 (
    .col0(out_36[15]), .col1(out_36[14]), .col2(out_36[13]), .col3(out_36[12]), .col4(out_36[11]),
    .col5(out_36[10]), .col6(out_36[9]), .col7(out_36[8]), .col8(out_36[7]), .col9(out_36[6]),
    .col10(out_36[5]), .col11(out_36[4]), .col12(out_36[3]), .col13(out_36[2]), .col14(out_36[1]),
    .col15(out_36[0]));
  DotMatrix #(.matrixcols(16), .matrixrows(1)) dotmatrix_5 (
    .col0(out_45[15]), .col1(out_45[14]), .col2(out_45[13]), .col3(out_45[12]), .col4(out_45[11]),
    .col5(out_45[10]), .col6(out_45[9]), .col7(out_45[8]), .col8(out_45[7]), .col9(out_45[6]),
    .col10(out_45[5]), .col11(out_45[4]), .col12(out_45[3]), .col13(out_45[2]), .col14(out_45[1]),
    .col15(out_45[0]));
  DotMatrix #(.matrixcols(16), .matrixrows(1)) dotmatrix_6 (
    .col0(out_52[15]), .col1(out_52[14]), .col2(out_52[13]), .col3(out_52[12]), .col4(out_52[11]),
    .col5(out_52[10]), .col6(out_52[9]), .col7(out_52[8]), .col8(out_52[7]), .col9(out_52[6]),
    .col10(out_52[5]), .col11(out_52[4]), .col12(out_52[3]), .col13(out_52[2]), .col14(out_52[1]),
    .col15(out_52[0]));
  DotMatrix #(.matrixcols(16), .matrixrows(1)) dotmatrix_7 (
    .col0(out_54[15]), .col1(out_54[14]), .col2(out_54[13]), .col3(out_54[12]), .col4(out_54[11]),
    .col5(out_54[10]), .col6(out_54[9]), .col7(out_54[8]), .col8(out_54[7]), .col9(out_54[6]),
    .col10(out_54[5]), .col11(out_54[4]), .col12(out_54[3]), .col13(out_54[2]), .col14(out_54[1]),
    .col15(out_54[0]));
  DotMatrix #(.matrixcols(16), .matrixrows(1)) dotmatrix_8 (
    .col0(out_56[15]), .col1(out_56[14]), .col2(out_56[13]), .col3(out_56[12]), .col4(out_56[11]),
    .col5(out_56[10]), .col6(out_56[9]), .col7(out_56[8]), .col8(out_56[7]), .col9(out_56[6]),
    .col10(out_56[5]), .col11(out_56[4]), .col12(out_56[3]), .col13(out_56[2]), .col14(out_56[1]),
    .col15(out_56[0]));
  DotMatrix #(.matrixcols(16), .matrixrows(1)) dotmatrix_9 (
    .col0(out_60[15]), .col1(out_60[14]), .col2(out_60[13]), .col3(out_60[12]), .col4(out_60[11]),
    .col5(out_60[10]), .col6(out_60[9]), .col7(out_60[8]), .col8(out_60[7]), .col9(out_60[6]),
    .col10(out_60[5]), .col11(out_60[4]), .col12(out_60[3]), .col13(out_60[2]), .col14(out_60[1]),
    .col15(out_60[0]));
  // Probe on out_13
  // Probe on out_20
  // Probe on out_26
  // Probe on out_36
  // Probe on out_45
  // Probe on out_52
  // Probe on out_54
  // Probe on out_56
  // Probe on out_60
  CPU cpu_1 (
    .out_10(out_10), .out_14(out_13), .out_19(out_17), .out_22(out_20), .out_28(out_26), .out_38(out_36),
    .out_47(out_45), .out_52(out_50), .out_54(out_52), .out_55(out_53), .in_1(RESET), .out_56(out_54),
    .in_2(multiplexer_1_out), .out_58(out_56), .DATA_2(DATA), .out_7(out_7), .out_8(out_8), .out_9(out_9),
    .out_11(out_11), .out_12(out_12), .out_15(out_14), .out_16(out_15), .out_18(out_16), .out_20(out_18),
    .out_23(out_21), .out_21(out_19), .out_25(out_23), .out_26(out_24), .out_24(out_22), .out_27(out_25),
    .out_30(out_28), .out_31(out_29), .out_29(out_27), .out_33(out_31), .out_34(out_32), .out_32(out_30),
    .out_35(out_33), .out_37(out_35), .out_36(out_34), .out_39(out_37), .out_40(out_38), .out_41(out_39),
    .out_43(out_41), .out_42(out_40), .out_44(out_42), .out_45(out_43), .out_46(out_44), .out_48(out_46),
    .out_49(out_47), .out_50(out_48), .out_51(out_49), .out_53(out_51), .out_57(out_55), .out_59(out_57),
    .out_60(out_58), .out_61(out_59), .out_63(out_61), .out_65(out_62), .DATA(DATA), .out_62(out_60),
    .out_13(cpu_1_out_13), .out_17(cpu_1_out_17), .in_3(in_2), .in_4(in_5), .in_5(in_6), .out_64(cpu_1_out_64));  // open: out_66
  // Probe on out_13
  // Probe on out_13
  // Probe on out_20
  // Probe on out_20
  // Probe on out_26
  // Probe on out_26
  // Probe on out_36
  // Probe on out_36
  // Probe on out_45
  // Probe on out_45
  // Probe on out_52
  // Probe on out_52
  // Probe on out_54
  // Probe on out_54
  // Probe on out_56
  // Probe on out_56
  // Probe on out_60
  // Probe on out_60
  RAM ram_1 (
    .data_in(DATA), .address(out_60), .output_enable(cpu_1_out_17), .input_enable(cpu_1_out_13),
    .clock(cpu_1_out_64), .tristate_data_out(DATA), .chip_enable(1'b1));  // open: addressed_value
  DotMatrix #(.matrixcols(16), .matrixrows(1)) dotmatrix_10 (
    .col0(out_10[15]), .col1(out_10[14]), .col2(out_10[13]), .col3(out_10[12]), .col4(out_10[11]),
    .col5(out_10[10]), .col6(out_10[9]), .col7(out_10[8]), .col8(out_10[7]), .col9(out_10[6]),
    .col10(out_10[5]), .col11(out_10[4]), .col12(out_10[3]), .col13(out_10[2]), .col14(out_10[1]),
    .col15(out_10[0]));
  DotMatrix #(.matrixcols(16), .matrixrows(1)) dotmatrix_11 (
    .col0(out_17[15]), .col1(out_17[14]), .col2(out_17[13]), .col3(out_17[12]), .col4(out_17[11]),
    .col5(out_17[10]), .col6(out_17[9]), .col7(out_17[8]), .col8(out_17[7]), .col9(out_17[6]),
    .col10(out_17[5]), .col11(out_17[4]), .col12(out_17[3]), .col13(out_17[2]), .col14(out_17[1]),
    .col15(out_17[0]));
  DotMatrix #(.matrixcols(16), .matrixrows(1)) dotmatrix_12 (
    .col0(out_50[15]), .col1(out_50[14]), .col2(out_50[13]), .col3(out_50[12]), .col4(out_50[11]),
    .col5(out_50[10]), .col6(out_50[9]), .col7(out_50[8]), .col8(out_50[7]), .col9(out_50[6]),
    .col10(out_50[5]), .col11(out_50[4]), .col12(out_50[3]), .col13(out_50[2]), .col14(out_50[1]),
    .col15(out_50[0]));
  LED led_30 (.in(out_53[2]));
  LED led_31 (.in(out_55));
  LED led_32 (.in(out_57));
  LED led_33 (.in(out_58));
  LED led_34 (.in(out_59));
  LED led_35 (.in(out_61));
  LED led_36 (.in(out_62));
  LED led_37 (.in(out_22));
  LED led_38 (.in(out_25));
  LED led_39 (.in(out_27));
  LED led_40 (.in(out_30));
  LED led_41 (.in(out_34));
  LED led_42 (.in(out_38));
  LED led_43 (.in(out_40));
  LED led_44 (.in(out_43));
  LED led_45 (.in(out_53[0]));
  LED led_46 (.in(out_53[1]));
  // Probe on out_10
  // Probe on out_10
  // Probe on out_10
  // Probe on out_17
  // Probe on out_17
  // Probe on out_17
  // Probe on out_50
  // Probe on out_50
  // Probe on out_50
  // Probe on out_53
  // Probe on out_53
  // Probe on out_53

  // Other names for the same wires on the sheet: A[15:0] = out_52; A_IN = out_11; A_OUT = out_14; ACC[15:0] = out_45;
  //   ACC_IN = out_7; ACC_OUT = out_9; ADDR_BUS_OUTPUT_ENABLE = in_5; ADDRESS[15:0] = out_60; ALU_A_IS_BUS = out_37;
  //   ALU_C_IN = out_51; ALU_CARRYBORROW_FLAG_CLOCKED = out_40; ALU_CARRYBORROW_FLAG_IMM = out_27;
  //   ALU_EQUAL_FLAG_CLOCKED = out_43; ALU_EQUAL_FLAG_IMM = out_30; ALU_M = out_48;
  //   ALU_NEGATIVE_FLAG_CLOCKED = out_38; ALU_NEGATIVE_FLAG_IMM = out_25; ALU_OUT = out_33;
  //   ALU_RESULT_CLOCKED[15:0] = out_17; ALU_RESULT_IMM[15:0] = out_10; ALU_S0 = out_39; ALU_S1 = out_42;
  //   ALU_S2 = out_44; ALU_S3 = out_47; ALU_STORE_FLAGS = out_31; ALU_STORE_RESULT = out_28;
  //   ALU_ZERO_FLAG_CLOCKED = out_34; ALU_ZERO_FLAG_IMM = out_22; B[15:0] = out_54; B_IN = out_16; B_OUT = out_18;
  //   BUS[15:0] = out_13; C[15:0] = out_56; C_IN = out_21; C_OUT = out_23; CLOCK_ENABLE = in_2; CLOCK_HALT = out_49;
  //   CONTROL_CLOCK = out_62; CU_CARRYBORROW_MIRROR = out_58; CU_EQUAL_MIRROR = out_59;
  //   CU_INSTRUCTION_MIRROR[15:0] = out_50; CU_MICROCODE_STEP[2:0] = out_53; CU_NEGATIVE_MIRROR = out_57;
  //   CU_STEP_RESET = out_46; CU_ZERO_MIRROR = out_55; DATA_BUS_OUTPUT_ENABLE = in_6; DATA_CLOCK = out_61;
  //   IR[15:0] = out_26; IR_IN = out_41; MANUAL_AUTO_CLOCK_SEL = in_3; MAR_IN = out_8; PC[15:0] = out_20;
  //   PC_COUNT = out_35; PC_IN = out_29; PC_OUT = out_32; READ_FROM_MEM = out_15; SP[15:0] = out_36; SP_IN = out_19;
  //   SP_OUT = out_24; WRITE_TO_MEM = out_12

  // Notes on the sheet:
  //   BIN
  //   HEX
  //   DEC
  //   BIN
  //   HEX
  //   DEC
  //   BIN
  //   HEX
  //   DEC
  //   BIN
  //   HEX
  //   DEC
  //   BIN
  //   HEX
  //   DEC
  //   BIN
  //   HEX
  //   DEC
  //   BIN
  //   HEX
  //   DEC
  //   BIN
  //   HEX
  //   DEC
  //   BIN
  //   HEX
  //   DEC
  //   BIN
  //   HEX
  //   DEC
  //   BIN
  //   HEX
  //   DEC
  //   BIN
  //   HEX
  //   DEC
  //   BIN
  //   HEX
  //   DEC
endmodule

module CPU (
  input  in_1,
  input  in_2,
  input  in_3,
  input  in_4,
  input  in_5,
  input  [15:0] DATA,
  output out_7,
  output out_8,
  output out_9,
  output [15:0] out_10,
  output out_11,
  output out_12,
  output out_13,
  output [15:0] out_14,
  output out_15,
  output out_16,
  output out_17,
  output out_18,
  output [15:0] out_19,
  output out_20,
  output out_21,
  output [15:0] out_22,
  output out_23,
  output out_24,
  output out_25,
  output out_26,
  output out_27,
  output [15:0] out_28,
  output out_29,
  output out_30,
  output out_31,
  output out_32,
  output out_33,
  output out_34,
  output out_35,
  output out_36,
  output out_37,
  output [15:0] out_38,
  output out_39,
  output out_40,
  output out_41,
  output out_42,
  output out_43,
  output out_44,
  output out_45,
  output out_46,
  output [15:0] out_47,
  output out_48,
  output out_49,
  output out_50,
  output out_51,
  output [15:0] out_52,
  output out_53,
  output [15:0] out_54,
  output [2:0] out_55,
  output [15:0] out_56,
  output out_57,
  output [15:0] out_58,
  output out_59,
  output out_60,
  output out_61,
  output [15:0] out_62,
  output out_63,
  output out_64,
  output out_65,
  output out_66,
  output [15:0] DATA_2
);

  wire and_1_out, and_2_out, and_3_out, j_k_ff_1_q, j_k_ff_1_qn, j_k_ff_2_q, j_k_ff_3_q, nor_1_out,
       nor_2_out, not_1_out, not_2_out, not_4_out, safe_clock_enable_1_clock_out, SIM_ONLY_RESET;
  wire [15:0] multiplexer_1_out, register_bus_r_2_content;

  Button button_1 (.out(SIM_ONLY_RESET));
  Pull_Resistor #(.pull(1)) pull_resistor_1 (.node(in_4));
  Pull_Resistor #(.pull(1)) pull_resistor_2 (.node(in_5));
  LED led_1 (.in(out_7));
  LED led_2 (.in(out_9));
  LED led_3 (.in(out_11));
  LED led_4 (.in(out_15));
  LED led_5 (.in(out_18));
  LED led_6 (.in(out_20));
  LED led_7 (.in(out_23));
  LED led_8 (.in(out_25));
  LED led_9 (.in(out_30));
  LED led_10 (.in(out_33));
  LED led_11 (.in(out_35));
  LED led_12 (.in(out_39));
  LED led_13 (.in(out_41));
  LED led_14 (.in(out_44));
  LED led_15 (.in(out_46));
  LED led_16 (.in(out_49));
  LED led_17 (.in(out_50));
  LED led_18 (.in(out_53));
  Pull_Resistor pull_resistor_3 (.node(out_62));
  assign out_62 = in_4 ? register_bus_r_2_content : 16'bz;  // Controlled_Buffer controlled_buffer_1
  nor nor_1 (nor_1_out, in_1, out_51);
  not not_1 (not_1_out, out_51);
  not not_2 (not_2_out, in_1);
  LED led_19 (.in(out_8));
  LED led_20 (.in(out_12));
  LED led_21 (.in(out_16));
  LED led_22 (.in(out_21));
  LED led_23 (.in(out_26));
  LED led_24 (.in(out_31));
  LED led_25 (.in(out_34));
  LED led_26 (.in(out_37));
  LED led_27 (.in(out_43));
  LED led_28 (.in(out_48));
  LED led_29 (.in(out_51));
  safe_clock_enable safe_clock_enable_1 (
    .clock_enable(nor_1_out), .clock_in(in_2), .clock_out(safe_clock_enable_1_clock_out));
  and and_1 (and_1_out, not_1_out, in_3);
  and and_2 (and_2_out, and_1_out, not_2_out);
  J_K_Flip_Flop j_k_ff_1 (
    .J(1'b1), .clk(safe_clock_enable_1_clock_out), .K(1'b1), .Q(j_k_ff_1_q), .Qn(j_k_ff_1_qn), .preset(1'b0),
    .en(1'b1), .reset(in_1));
  safe_clock_enable_disable safe_clock_enable_disable_1 (.clock_enable(and_2_out), .clock_in(in_2), .clock_out(out_63));
  DotMatrix #(.matrixcols(16), .matrixrows(1)) dotmatrix_1 (
    .col0(out_14[15]), .col1(out_14[14]), .col2(out_14[13]), .col3(out_14[12]), .col4(out_14[11]),
    .col5(out_14[10]), .col6(out_14[9]), .col7(out_14[8]), .col8(out_14[7]), .col9(out_14[6]),
    .col10(out_14[5]), .col11(out_14[4]), .col12(out_14[3]), .col13(out_14[2]), .col14(out_14[1]),
    .col15(out_14[0]));
  DotMatrix #(.matrixcols(16), .matrixrows(1)) dotmatrix_2 (
    .col0(out_22[15]), .col1(out_22[14]), .col2(out_22[13]), .col3(out_22[12]), .col4(out_22[11]),
    .col5(out_22[10]), .col6(out_22[9]), .col7(out_22[8]), .col8(out_22[7]), .col9(out_22[6]),
    .col10(out_22[5]), .col11(out_22[4]), .col12(out_22[3]), .col13(out_22[2]), .col14(out_22[1]),
    .col15(out_22[0]));
  DotMatrix #(.matrixcols(16), .matrixrows(1)) dotmatrix_3 (
    .col0(out_28[15]), .col1(out_28[14]), .col2(out_28[13]), .col3(out_28[12]), .col4(out_28[11]),
    .col5(out_28[10]), .col6(out_28[9]), .col7(out_28[8]), .col8(out_28[7]), .col9(out_28[6]),
    .col10(out_28[5]), .col11(out_28[4]), .col12(out_28[3]), .col13(out_28[2]), .col14(out_28[1]),
    .col15(out_28[0]));
  DotMatrix #(.matrixcols(16), .matrixrows(1)) dotmatrix_4 (
    .col0(out_38[15]), .col1(out_38[14]), .col2(out_38[13]), .col3(out_38[12]), .col4(out_38[11]),
    .col5(out_38[10]), .col6(out_38[9]), .col7(out_38[8]), .col8(out_38[7]), .col9(out_38[6]),
    .col10(out_38[5]), .col11(out_38[4]), .col12(out_38[3]), .col13(out_38[2]), .col14(out_38[1]),
    .col15(out_38[0]));
  DotMatrix #(.matrixcols(16), .matrixrows(1)) dotmatrix_5 (
    .col0(out_47[15]), .col1(out_47[14]), .col2(out_47[13]), .col3(out_47[12]), .col4(out_47[11]),
    .col5(out_47[10]), .col6(out_47[9]), .col7(out_47[8]), .col8(out_47[7]), .col9(out_47[6]),
    .col10(out_47[5]), .col11(out_47[4]), .col12(out_47[3]), .col13(out_47[2]), .col14(out_47[1]),
    .col15(out_47[0]));
  DotMatrix #(.matrixcols(16), .matrixrows(1)) dotmatrix_6 (
    .col0(out_54[15]), .col1(out_54[14]), .col2(out_54[13]), .col3(out_54[12]), .col4(out_54[11]),
    .col5(out_54[10]), .col6(out_54[9]), .col7(out_54[8]), .col8(out_54[7]), .col9(out_54[6]),
    .col10(out_54[5]), .col11(out_54[4]), .col12(out_54[3]), .col13(out_54[2]), .col14(out_54[1]),
    .col15(out_54[0]));
  DotMatrix #(.matrixcols(16), .matrixrows(1)) dotmatrix_7 (
    .col0(out_56[15]), .col1(out_56[14]), .col2(out_56[13]), .col3(out_56[12]), .col4(out_56[11]),
    .col5(out_56[10]), .col6(out_56[9]), .col7(out_56[8]), .col8(out_56[7]), .col9(out_56[6]),
    .col10(out_56[5]), .col11(out_56[4]), .col12(out_56[3]), .col13(out_56[2]), .col14(out_56[1]),
    .col15(out_56[0]));
  DotMatrix #(.matrixcols(16), .matrixrows(1)) dotmatrix_8 (
    .col0(out_58[15]), .col1(out_58[14]), .col2(out_58[13]), .col3(out_58[12]), .col4(out_58[11]),
    .col5(out_58[10]), .col6(out_58[9]), .col7(out_58[8]), .col8(out_58[7]), .col9(out_58[6]),
    .col10(out_58[5]), .col11(out_58[4]), .col12(out_58[3]), .col13(out_58[2]), .col14(out_58[1]),
    .col15(out_58[0]));
  DotMatrix #(.matrixcols(16), .matrixrows(1)) dotmatrix_9 (
    .col0(out_62[15]), .col1(out_62[14]), .col2(out_62[13]), .col3(out_62[12]), .col4(out_62[11]),
    .col5(out_62[10]), .col6(out_62[9]), .col7(out_62[8]), .col8(out_62[7]), .col9(out_62[6]),
    .col10(out_62[5]), .col11(out_62[4]), .col12(out_62[3]), .col13(out_62[2]), .col14(out_62[1]),
    .col15(out_62[0]));
  control_unit control_unit_1 (
    .mirror_instruction(out_52), .instruction(out_28), .equal_flag(out_45), .carryborrow_flag(out_42),
    .negative_flag(out_40), .zero_flag(out_36), .mirror_equal_flag(out_61), .mirror_carryborrow_flag(out_60),
    .mirror_negative_flag(out_59), .mirror_zero_flag(out_57), .microcode_step(out_55),
    .control_clock(out_65), .reset(in_1), .sim_only_clear(SIM_ONLY_RESET), .CLOCK_HALT(out_51),
    .CU_STEP_RESET(out_48), .IR_IN(out_43), .PC_COUNT(out_37), .PC_OUT(out_34), .PC_IN(out_31),
    .SP_OUT(out_26), .SP_IN(out_21), .READ_FROM_MEM(out_16), .WRITE_TO_MEM(out_12), .MAR_IN(out_8),
    .ALU_C_IN(out_53), .ALU_M(out_50), .ALU_S3(out_49), .ALU_S2(out_46), .ALU_S1(out_44), .ALU_S0(out_41),
    .ALU_A_IS_BUS(out_39), .ALU_OUT(out_35), .ALU_STORE_FLAGS(out_33), .ALU_STORE_RESULT(out_30),
    .C_OUT(out_25), .C_IN(out_23), .B_OUT(out_20), .B_IN(out_18), .A_OUT(out_15), .A_IN(out_11),
    .ACC_OUT(out_9), .ACC_IN(out_7));
  nor nor_2 (nor_2_out, out_16, and_3_out);
  and and_3 (and_3_out, out_12, in_5);
  register_bus_R register_bus_r_1 (
    .\input (out_14), .input_enable(out_43), .clock(out_63), .buffered_output(out_14), .content(out_28),
    .sim_only_reset(SIM_ONLY_RESET), .output_enable(1'b0));
  register_bus_R register_bus_r_2 (
    .\input (out_14), .input_enable(out_8), .clock(out_63), .content(register_bus_r_2_content),
    .sim_only_reset(SIM_ONLY_RESET), .output_enable(1'b0));  // open: buffered_output
  J_K_Flip_Flop j_k_ff_2 (
    .J(1'b1), .clk(j_k_ff_1_q), .K(1'b1), .Q(j_k_ff_2_q), .preset(1'b0), .en(1'b1), .reset(in_1));  // open: Qn
  not not_3 (out_65, out_63);
  // Probe on out_14
  // Probe on out_22
  // Probe on out_28
  // Probe on out_38
  // Probe on out_47
  // Probe on out_54
  // Probe on out_56
  // Probe on out_58
  // Probe on out_62
  not not_4 (not_4_out, nor_2_out);
  // Probe on out_14
  // Probe on out_14
  // Probe on out_22
  // Probe on out_22
  // Probe on out_28
  // Probe on out_28
  // Probe on out_38
  // Probe on out_38
  // Probe on out_47
  // Probe on out_47
  // Probe on out_54
  // Probe on out_54
  // Probe on out_56
  // Probe on out_56
  // Probe on out_58
  // Probe on out_58
  // Probe on out_62
  // Probe on out_62
  J_K_Flip_Flop j_k_ff_3 (
    .J(1'b1), .clk(j_k_ff_1_qn), .K(1'b1), .Q(j_k_ff_3_q), .preset(1'b0), .en(1'b1), .reset(in_1));  // open: Qn
  Pull_Resistor pull_resistor_4 (.node(DATA_2));
  assign DATA_2 = not_4_out ? out_14 : 16'bz;  // Controlled_Buffer controlled_buffer_2
  Pull_Resistor pull_resistor_5 (.node(DATA));
  assign out_14 = not_4_out ? DATA : 16'bz;  // Controlled_Buffer controlled_buffer_3
  DotMatrix #(.matrixcols(16), .matrixrows(1)) dotmatrix_10 (
    .col0(out_10[15]), .col1(out_10[14]), .col2(out_10[13]), .col3(out_10[12]), .col4(out_10[11]),
    .col5(out_10[10]), .col6(out_10[9]), .col7(out_10[8]), .col8(out_10[7]), .col9(out_10[6]),
    .col10(out_10[5]), .col11(out_10[4]), .col12(out_10[3]), .col13(out_10[2]), .col14(out_10[1]),
    .col15(out_10[0]));
  DotMatrix #(.matrixcols(16), .matrixrows(1)) dotmatrix_11 (
    .col0(out_19[15]), .col1(out_19[14]), .col2(out_19[13]), .col3(out_19[12]), .col4(out_19[11]),
    .col5(out_19[10]), .col6(out_19[9]), .col7(out_19[8]), .col8(out_19[7]), .col9(out_19[6]),
    .col10(out_19[5]), .col11(out_19[4]), .col12(out_19[3]), .col13(out_19[2]), .col14(out_19[1]),
    .col15(out_19[0]));
  DotMatrix #(.matrixcols(16), .matrixrows(1)) dotmatrix_12 (
    .col0(out_52[15]), .col1(out_52[14]), .col2(out_52[13]), .col3(out_52[12]), .col4(out_52[11]),
    .col5(out_52[10]), .col6(out_52[9]), .col7(out_52[8]), .col8(out_52[7]), .col9(out_52[6]),
    .col10(out_52[5]), .col11(out_52[4]), .col12(out_52[3]), .col13(out_52[2]), .col14(out_52[1]),
    .col15(out_52[0]));
  LED led_30 (.in(out_55[2]));
  LED led_31 (.in(out_57));
  LED led_32 (.in(out_59));
  LED led_33 (.in(out_60));
  LED led_34 (.in(out_61));
  LED led_35 (.in(out_63));
  LED led_36 (.in(out_65));
  Pull_Resistor pull_resistor_6 (.node(out_14));
  LED led_37 (.in(out_24));
  LED led_38 (.in(out_27));
  LED led_39 (.in(out_29));
  LED led_40 (.in(out_32));
  LED led_41 (.in(out_36));
  LED led_42 (.in(out_40));
  LED led_43 (.in(out_42));
  LED led_44 (.in(out_45));
  LED led_45 (.in(out_55[1]));
  LED led_46 (.in(out_55[0]));
  Multiplexer #(.width(16), .enable("false")) multiplexer_1 (
    .in0(out_47), .in1(out_14), .out(multiplexer_1_out), .sel(out_39));
  ALU alu_1 (
    .carry_in(out_53), .M(out_50), .S0(out_41), .S1(out_44), .S2(out_46), .S3(out_49), .clock(out_63),
    .store_result(out_30), .store_flags(out_33), .unclocked_zero(out_24), .clocked_zero(out_36),
    .unclocked_negative(out_27), .clocked_negative(out_40), .unclocked_carryborrow_out(out_29),
    .clocked_carryborrow_out(out_42), .unclocked_A___B(out_32), .clocked_A___B(out_45),
    .tristate_clocked_result(out_14), .sim_only_reset(SIM_ONLY_RESET), .A(multiplexer_1_out), .B(out_14),
    .result_output_enable(out_35), .unclocked_result(out_10), .clocked_result(out_19));
  // Probe on out_10
  // Probe on out_10
  // Probe on out_10
  // Probe on out_19
  // Probe on out_19
  // Probe on out_19
  // Probe on out_52
  // Probe on out_52
  // Probe on out_52
  // Probe on out_55
  // Probe on out_55
  // Probe on out_55
  program_counter program_counter_1 (
    .\input (out_14), .count(out_37), .clock(out_63), .reset(in_1), .output_enable(out_34),
    .tristate_output(out_14), .contents(out_22), .in(out_31));
  register_bus_L register_bus_l_1 (
    .\input (out_14), .input_enable(out_7), .clock(out_63), .buffered_output(out_14), .content(out_47),
    .sim_only_reset(SIM_ONLY_RESET), .output_enable(out_9));
  register_bus_L register_bus_l_2 (
    .\input (out_14), .input_enable(out_11), .clock(out_63), .buffered_output(out_14), .content(out_54),
    .sim_only_reset(SIM_ONLY_RESET), .output_enable(out_15));
  register_bus_L register_bus_l_3 (
    .\input (out_14), .input_enable(out_18), .clock(out_63), .buffered_output(out_14), .content(out_56),
    .sim_only_reset(SIM_ONLY_RESET), .output_enable(out_20));
  register_bus_L register_bus_l_4 (
    .\input (out_14), .input_enable(out_23), .clock(out_63), .buffered_output(out_14), .content(out_58),
    .sim_only_reset(SIM_ONLY_RESET), .output_enable(out_25));
  register_bus_L register_bus_l_5 (
    .\input (out_14), .input_enable(out_21), .clock(out_63), .buffered_output(out_14), .content(out_38),
    .sim_only_reset(SIM_ONLY_RESET), .output_enable(out_26));

  assign out_13 = out_12;
  assign out_17 = out_16;
  assign out_64 = out_63;
  assign out_66 = out_65;

  // Other names for the same wires on the sheet: A[15:0] = out_54; A_IN = out_11; A_OUT = out_15; ACC[15:0] = out_47;
  //   ACC_IN = out_7; ACC_OUT = out_9; ADDR_BUS_OUTPUT_ENABLE = in_4; ADDRESS[15:0] = out_62; ALU_A_IS_BUS = out_39;
  //   ALU_C_IN = out_53; ALU_CARRYBORROW_FLAG_CLOCKED = out_42; ALU_CARRYBORROW_FLAG_IMM = out_29;
  //   ALU_EQUAL_FLAG_CLOCKED = out_45; ALU_EQUAL_FLAG_IMM = out_32; ALU_M = out_50;
  //   ALU_NEGATIVE_FLAG_CLOCKED = out_40; ALU_NEGATIVE_FLAG_IMM = out_27; ALU_OUT = out_35;
  //   ALU_RESULT_CLOCKED[15:0] = out_19; ALU_RESULT_IMM[15:0] = out_10; ALU_S0 = out_41; ALU_S1 = out_44;
  //   ALU_S2 = out_46; ALU_S3 = out_49; ALU_STORE_FLAGS = out_33; ALU_STORE_RESULT = out_30;
  //   ALU_ZERO_FLAG_CLOCKED = out_36; ALU_ZERO_FLAG_IMM = out_24; B[15:0] = out_56; B_IN = out_18; B_OUT = out_20;
  //   BUS[15:0] = out_14; C[15:0] = out_58; C_IN = out_23; C_OUT = out_25; CLOCK_ENABLE = in_3; CLOCK_HALT = out_51;
  //   CONTROL_CLOCK = out_65; CU_CARRYBORROW_MIRROR = out_60; CU_EQUAL_MIRROR = out_61;
  //   CU_INSTRUCTION_MIRROR[15:0] = out_52; CU_MICROCODE_STEP[2:0] = out_55; CU_NEGATIVE_MIRROR = out_59;
  //   CU_STEP_RESET = out_48; CU_ZERO_MIRROR = out_57; DATA_BUS_OUTPUT_ENABLE = in_5; DATA_CLOCK = out_63;
  //   EXT_CLOCK_PULSE = in_2; IR[15:0] = out_28; IR_IN = out_43; MAR_IN = out_8; PC[15:0] = out_22; PC_COUNT = out_37;
  //   PC_IN = out_31; PC_OUT = out_34; READ_FROM_MEM = out_16; RESET = in_1; SP[15:0] = out_38; SP_IN = out_21;
  //   SP_OUT = out_26; WRITE_TO_MEM = out_12

  // Notes on the sheet:
  //   BIN
  //   HEX
  //   DEC
  //   BIN
  //   HEX
  //   DEC
  //   BIN
  //   HEX
  //   DEC
  //   BIN
  //   HEX
  //   DEC
  //   BIN
  //   HEX
  //   DEC
  //   BIN
  //   HEX
  //   DEC
  //   BIN
  //   HEX
  //   DEC
  //   BIN
  //   HEX
  //   DEC
  //   BIN
  //   HEX
  //   DEC
  //   BIN
  //   HEX
  //   DEC
  //   BIN
  //   HEX
  //   DEC
  //   BIN
  //   HEX
  //   DEC
  //   BIN
  //   HEX
  //   DEC
endmodule

module RAM (
  input  [15:0] data_in,
  input  [15:0] address,
  input  chip_enable,
  input  output_enable,
  input  input_enable,
  input  clock,
  output [15:0] addressed_value,
  output [15:0] tristate_data_out
);

  wire multiplexer_1_out, multiplexer_2_out, not_1_out, safe_clock_enable_1_clock_out;

  Multiplexer multiplexer_1 (.in0(1'b0), .in1(input_enable), .out(multiplexer_1_out), .sel(chip_enable), .en(1'b1));
  safe_clock_enable safe_clock_enable_1 (
    .clock_enable(multiplexer_1_out), .clock_in(clock), .clock_out(safe_clock_enable_1_clock_out));
  Multiplexer multiplexer_2 (.in0(1'b0), .in1(output_enable), .out(multiplexer_2_out), .sel(chip_enable), .en(1'b1));
  RAM_part #(.addrWidth(16), .dataWidth(16)) ram_1 (
    .addr(address), .data(addressed_value), .sel(1'b1), .clk(safe_clock_enable_1_clock_out), .ld(not_1_out),
    .clr(1'b0));
  assign addressed_value = multiplexer_1_out ? data_in : 16'bz;  // Controlled_Buffer controlled_buffer_1
  not not_1 (not_1_out, multiplexer_1_out);
  assign tristate_data_out = multiplexer_2_out ? addressed_value : 16'bz;  // Controlled_Buffer controlled_buffer_2
endmodule

module control_unit (
  input  [15:0] instruction,
  input  equal_flag,
  input  carryborrow_flag,
  input  negative_flag,
  input  zero_flag,
  input  control_clock,
  input  reset,
  input  sim_only_clear,
  output [15:0] mirror_instruction,
  output CLOCK_HALT,
  output CU_STEP_RESET,
  output IR_IN,
  output PC_COUNT,
  output PC_OUT,
  output PC_IN,
  output SP_OUT,
  output SP_IN,
  output mirror_equal_flag,
  output READ_FROM_MEM,
  output mirror_carryborrow_flag,
  output WRITE_TO_MEM,
  output mirror_negative_flag,
  output MAR_IN,
  output mirror_zero_flag,
  output ALU_C_IN,
  output ALU_M,
  output [2:0] microcode_step,
  output ALU_S3,
  output ALU_S2,
  output ALU_S1,
  output ALU_S0,
  output ALU_A_IS_BUS,
  output ALU_OUT,
  output ALU_STORE_FLAGS,
  output ALU_STORE_RESULT,
  output C_OUT,
  output C_IN,
  output B_OUT,
  output B_IN,
  output A_OUT,
  output A_IN,
  output ACC_OUT,
  output ACC_IN
);

  wire not_1_out;
  wire [7:5] rom_1_data;

  not not_1 (not_1_out, CU_STEP_RESET);
  Register u_mirror_instruction (
    .D(instruction[7:0]), .en(1'b1), .Q(mirror_instruction[7:0]), .clk(control_clock), .clr(sim_only_clear));
  Register #(.width(4)) mirror_flags (
    .D({equal_flag, carryborrow_flag, negative_flag, zero_flag}), .en(1'b1),
    .Q({mirror_equal_flag, mirror_carryborrow_flag, mirror_negative_flag, mirror_zero_flag}),
    .clk(control_clock), .clr(sim_only_clear));
  Counter #(.width(3), .max('h7)) microcode_step_counter (
    .load(CU_STEP_RESET), .D(3'b000), .count(not_1_out), .Q(microcode_step), .clk(control_clock), .clr(reset));  // open: carry
  ROM #(.addrWidth(15)) rom_1 (
    .addr({mirror_instruction[7:0], mirror_equal_flag, mirror_carryborrow_flag, mirror_negative_flag, mirror_zero_flag, microcode_step}),
    .data({rom_1_data, CLOCK_HALT, CU_STEP_RESET, IR_IN, PC_COUNT, PC_OUT}), .sel(1'b1));
  ROM #(.addrWidth(15)) rom_2 (
    .addr({mirror_instruction[7:0], mirror_equal_flag, mirror_carryborrow_flag, mirror_negative_flag, mirror_zero_flag, microcode_step}),
    .data({PC_IN, SP_OUT, SP_IN, READ_FROM_MEM, WRITE_TO_MEM, MAR_IN, ALU_C_IN, ALU_M}), .sel(1'b1));
  ROM #(.addrWidth(15)) rom_3 (
    .addr({mirror_instruction[7:0], mirror_equal_flag, mirror_carryborrow_flag, mirror_negative_flag, mirror_zero_flag, microcode_step}),
    .data({ALU_S3, ALU_S2, ALU_S1, ALU_S0, ALU_A_IS_BUS, ALU_OUT, ALU_STORE_FLAGS, ALU_STORE_RESULT}),
    .sel(1'b1));
  ROM #(.addrWidth(15)) rom_4 (
    .addr({mirror_instruction[7:0], mirror_equal_flag, mirror_carryborrow_flag, mirror_negative_flag, mirror_zero_flag, microcode_step}),
    .data({C_OUT, C_IN, B_OUT, B_IN, A_OUT, A_IN, ACC_OUT, ACC_IN}), .sel(1'b1));

  assign mirror_instruction[15:8] = {8{1'b0}};

  // Notes on the sheet:
  //   Common inputs to all EEPROMS
  //   microcode 3
  //   microcode 2
  //   microcode 1
  //   microcode 0
  //   contents of rom_1 (hex, n*v repeats v):
  //   1 6 0 8 4*0 1 6 0 8 4*0 1 6 0 8 4*0 1 6 0 8 4*0 1 6 0 8 4*0 1 6 0 8 4*0 1 6 0 8 4*0 1 6 0 8 4*0 1 6
  //   0 8 4*0 1 6 0 8 4*0 1 6 0 8 4*0 1 6 0 8 4*0 1 6 0 8 4*0 1 6 0 8 4*0 1 6 0 8 4*0 1 6 0 8 4*0 1 6 0 8
  //   4*0 1 6 0 8 4*0 1 6 0 8 4*0 1 6 0 8 4*0 1 6 0 8 4*0 1 6 0 8 4*0 1 6 0 8 4*0 1 6 0 8 4*0 1 6 0 8 4*0
  //   1 6 0 8 4*0 1 6 0 8 4*0 1 6 0 8 4*0 1 6 0 8 4*0 1 6 0 8 4*0 1 6 0 8 4*0 1 6 0 8 4*0 1 6 0 8 4*0 1 6
  //   0 8 4*0 1 6 0 8 4*0 1 6 0 8 4*0 1 6 0 8 4*0 1 6 0 8 4*0 1 6 0 8 4*0 1 6 0 8 4*0 1 6 0 8 4*0 1 6 0 8
  //   4*0 1 6 0 8 4*0 1 6 0 8 4*0 1 6 0 8 4*0 1 6 0 8 4*0 1 6 0 8 4*0 1 6 0 8 4*0 1 6 1 2 8 0 0 0 1 6 1 2
  //   8 0 0 0 1 6 1 2 8 0 0 0 1 6 1 2 8 0 0 0 1 6 1 2 8 0 0 0 1 6 1 2 8 0 0 0 1 6 1 2 8 0 0 0 1 6 1 2 8 0
  //   0 0 1 6 1 2 8 0 0 0 1 6 1 2 8 0 0 0 1 6 1 2 8 0 0 0 1 6 1 2 8 0 0 0 1 6 1 2 8 0 0 0 1 6 1 2 8 0 0 0
  //   1 6 1 2 8 0 0 0 1 6 1 2 8 0 0 0 1 6 1 2 0 0 8 0 1 6 1 2 0 0 8 0 1 6 1 2 0 0 8 0 1 6 1 2 0 0 8 0 1 6
  //   1 2 0 0 8 0 1 6 1 2 0 0 8 0 1 6 1 2 0 0 8 0 1 6 1 2 0 0 8 0 1 6 1 2 0 0 8 0 1 6 1 2 0 0 8 0 1 6 1 2
  //   0 0 8 0 1 6 1 2 0 0 8 0 1 6 1 2 0 0 8 0 1 6 1 2 0 0 8 0 1 6 1 2 0 0 8 0 1 6 1 2 0 0 8 0 1 6 0 8 4*0
  //   1 6 0 8 4*0 1 6 0 8 4*0 1 6 0 8 4*0 1 6 0 8 4*0 1 6 0 8 4*0 1 6 0 8 4*0 1 6 0 8 4*0 1 6 0 8 4*0 1 6
  //   0 8 4*0 1 6 0 8 4*0 1 6 0 8 4*0 1 6 0 8 4*0 1 6 0 8 4*0 1 6 0 8 4*0 1 6 0 8 4*0 1 6 0 8 4*0 1 6 0 8
  //   4*0 1 6 0 8 4*0 1 6 0 8 4*0 1 6 0 8 4*0 1 6 0 8 4*0 1 6 0 8 4*0 1 6 0 8 4*0 1 6 0 8 4*0 1 6 0 8 4*0
  //   1 6 0 8 4*0 1 6 0 8 4*0 1 6 0 8 4*0 1 6 0 8 4*0 1 6 0 8 4*0 1 6 0 8 4*0 1 6 0 8 4*0 1 6 0 8 4*0 1 6
  //   0 8 4*0 1 6 0 8 4*0 1 6 0 8 4*0 1 6 0 8 4*0 1 6 0 8 4*0 1 6 0 8 4*0 1 6 0 8 4*0 1 6 0 8 4*0 1 6 0 8
  //   4*0 1 6 0 8 4*0 1 6 0 8 4*0 1 6 0 8 4*0 1 6 0 8 4*0 1 6 0 8 4*0 1 6 1 2 8 0 0 0 1 6 1 2 8 0 0 0 1 6
  //   1 2 8 0 0 0 1 6 1 2 8 0 0 0 1 6 1 2 8 0 0 0 1 6 1 2 8 0 0 0 1 6 1 2 8 0 0 0 1 6 1 2 8 0 0 0 1 6 1 2
  //   8 0 0 0 1 6 1 2 8 0 0 0 1 6 1 2 8 0 0 0 1 6 1 2 8 0 0 0 1 6 1 2 8 0 0 0 1 6 1 2 8 0 0 0 1 6 1 2 8 0
  //   0 0 1 6 1 2 8 0 0 0 1 6 1 2 0 0 8 0 1 6 1 2 0 0 8 0 1 6 1 2 0 0 8 0 1 6 1 2 0 0 8 0 1 6 1 2 0 0 8 0
  //   1 6 1 2 0 0 8 0 1 6 1 2 0 0 8 0 1 6 1 2 0 0 8 0 1 6 1 2 0 0 8 0 1 6 1 2 0 0 8 0 1 6 1 2 0 0 8 0 1 6
  //   1 2 0 0 8 0 1 6 1 2 0 0 8 0 1 6 1 2 0 0 8 0 1 6 1 2 0 0 8 0 1 6 1 2 0 0 8 0 1 6 0 8 4*0 1 6 0 8 4*0
  //   1 6 0 8 4*0 1 6 0 8 4*0 1 6 0 8 4*0 1 6 0 8 4*0 1 6 0 8 4*0 1 6 0 8 4*0 1 6 0 8 4*0 1 6 0 8 4*0 1 6
  //   0 8 4*0 1 6 0 8 4*0 1 6 0 8 4*0 1 6 0 8 4*0 1 6 0 8 4*0 1 6 0 8 4*0 1 6 0 8 4*0 1 6 0 8 4*0 1 6 0 8
  //   4*0 1 6 0 8 4*0 1 6 0 8 4*0 1 6 0 8 4*0 1 6 0 8 4*0 1 6 0 8 4*0 1 6 0 8 4*0 1 6 0 8 4*0 1 6 0 8 4*0
  //   1 6 0 8 4*0 1 6 0 8 4*0 1 6 0 8 4*0 1 6 0 8 4*0 1 6 0 8 4*0 1 6 0 8 4*0 1 6 0 8 4*0 1 6 0 8 4*0 1 6
  //   0 8 4*0 1 6 0 8 4*0 1 6 0 8 4*0 1 6 0 8 4*0 1 6 0 8 4*0 1 6 0 8 4*0 1 6 0 8 4*0 1 6 0 8 4*0 1 6 0 8
  //   4*0 1 6 0 8 4*0 1 6 0 8 4*0 1 6 0 8 4*0 1 6 0 8 4*0 1 6 0 8 4*0 1 6 0 8 4*0 1 6 0 8 4*0 1 6 0 8 4*0
  //   1 6 0 8 4*0 1 6 0 8 4*0 1 6 0 8 4*0 1 6 0 8 4*0 1 6 0 8 4*0 1 6 0 8 4*0 1 6 0 8 4*0 1 6 0 8 4*0 1 6
  //   0 8 4*0 1 6 0 8 4*0 1 6 0 8 4*0 1 6 0 8 4*0 1 6 0 8 4*0 1 6 0 8 4*0 1 6 0 8 4*0 1 6 0 8 4*0 1 6 0 8
  //   4*0 1 6 0 8 4*0 1 6 0 8 4*0 1 6 0 8 4*0 1 6 0 8 4*0 1 6 0 8 4*0 1 6 0 8 4*0 1 6 0 8 4*0 1 6 0 8 4*0
  //   1 6 0 8 4*0 1 6 0 8 4*0 1 6 0 8 4*0 1 6 0 8 4*0 1 6 0 8 4*0 1 6 0 8 4*0 1 6 0 8 4*0 1 6 0 8 4*0 1 6
  //   0 8 4*0 1 6 0 8 4*0 1 6 0 8 4*0 1 6 0 8 4*0 1 6 0 8 4*0 1 6 0 8 4*0 1 6 0 8 4*0 1 6 0 8 4*0 1 6 0 8
  //   4*0 1 6 0 8 4*0 1 6 0 8 4*0 1 6 0 8 4*0 1 6 0 8 4*0 1 6 0 8 4*0 1 6 0 8 4*0 1 6 0 8 4*0 1 6 0 8 4*0
  //   1 6 0 8 4*0 1 6 0 8 4*0 1 6 0 8 4*0 1 6 0 8 4*0 1 6 0 8 4*0 1 6 0 8 4*0 1 6 0 8 4*0 1 6 0 8 4*0 1 6
  //   0 8 4*0 1 6 0 8 4*0 1 6 0 8 4*0 1 6 0 8 4*0 1 6 0 8 4*0 1 6 0 8 4*0 1 6 0 8 4*0 1 6 0 8 4*0 1 6 0 8
  //   4*0 1 6 0 8 4*0 1 6 0 8 4*0 1 6 0 8 4*0 1 6 0 8 4*0 1 6 0 8 4*0 1 6 0 8 4*0 1 6 0 8 4*0 1 6 0 8 4*0
  //   1 6 0 8 4*0 1 6 0 8 4*0 1 6 0 8 4*0 1 6 0 8 4*0 1 6 0 8 4*0 1 6 0 8 4*0 1 6 0 8 4*0 1 6 0 8 4*0 1 6
  //   0 8 4*0 1 6 0 8 4*0 1 6 0 8 4*0 1 6 0 8 4*0 1 6 0 8 4*0 1 6 0 8 4*0 1 6 0 8 4*0 1 6 0 8 4*0 1 6 0 8
  //   4*0 1 6 0 8 4*0 1 6 0 8 4*0 1 6 0 8 4*0 1 6 0 8 4*0 1 6 0 8 4*0 1 6 0 8 4*0 1 6 0 8 4*0 1 6 0 8 4*0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
  //   contents of rom_2 (hex, n*v repeats v):
  //   4 10 6*0 4 10 6*0 4 10 6*0 4 10 6*0 4 10 6*0 4 10 6*0 4 10 6*0 4 10 6*0 4 10 6*0 4 10 6*0 4 10 6*0 4
  //   10 6*0 4 10 6*0 4 10 6*0 4 10 6*0 4 10 6*0 4 10 6*0 4 10 6*0 4 10 6*0 4 10 6*0 4 10 6*0 4 10 6*0 4
  //   10 6*0 4 10 6*0 4 10 6*0 4 10 6*0 4 10 6*0 4 10 6*0 4 10 6*0 4 10 6*0 4 10 6*0 4 10 6*0 4 10 6*0 4
  //   10 6*0 4 10 6*0 4 10 6*0 4 10 6*0 4 10 6*0 4 10 6*0 4 10 6*0 4 10 6*0 4 10 6*0 4 10 6*0 4 10 6*0 4
  //   10 6*0 4 10 6*0 4 10 6*0 4 10 6*0 4 10 4 10 4*0 4 10 4 10 4*0 4 10 4 10 4*0 4 10 4 10 4*0 4 10 4 10
  //   4*0 4 10 4 10 4*0 4 10 4 10 4*0 4 10 4 10 4*0 4 10 4 10 4*0 4 10 4 10 4*0 4 10 4 10 4*0 4 10 4 10
  //   4*0 4 10 4 10 4*0 4 10 4 10 4*0 4 10 4 10 4*0 4 10 4 10 4*0 4 10 4 10 4 10 0 0 4 10 4 10 4 10 0 0 4
  //   10 4 10 4 10 0 0 4 10 4 10 4 10 0 0 4 10 4 10 4 10 0 0 4 10 4 10 4 10 0 0 4 10 4 10 4 10 0 0 4 10 4
  //   10 4 10 0 0 4 10 4 10 4 10 0 0 4 10 4 10 4 10 0 0 4 10 4 10 4 10 0 0 4 10 4 10 4 10 0 0 4 10 4 10 4
  //   10 0 0 4 10 4 10 4 10 0 0 4 10 4 10 4 10 0 0 4 10 4 10 4 10 0 0 4 10 2 5*0 4 10 2 5*0 4 10 2 5*0 4
  //   10 2 5*0 4 10 2 5*0 4 10 2 5*0 4 10 2 5*0 4 10 2 5*0 4 10 2 5*0 4 10 2 5*0 4 10 2 5*0 4 10 2 5*0 4
  //   10 2 5*0 4 10 2 5*0 4 10 2 5*0 4 10 2 5*0 4 10 2 5*0 4 10 2 5*0 4 10 2 5*0 4 10 2 5*0 4 10 2 5*0 4
  //   10 2 5*0 4 10 2 5*0 4 10 2 5*0 4 10 2 5*0 4 10 2 5*0 4 10 2 5*0 4 10 2 5*0 4 10 2 5*0 4 10 2 5*0 4
  //   10 2 5*0 4 10 2 5*0 4 10 2 5*0 4 10 2 5*0 4 10 2 5*0 4 10 2 5*0 4 10 2 5*0 4 10 2 5*0 4 10 2 5*0 4
  //   10 2 5*0 4 10 2 5*0 4 10 2 5*0 4 10 2 5*0 4 10 2 5*0 4 10 2 5*0 4 10 2 5*0 4 10 2 5*0 4 10 2 5*0 4
  //   10 4 12 4*0 4 10 4 12 4*0 4 10 4 12 4*0 4 10 4 12 4*0 4 10 4 12 4*0 4 10 4 12 4*0 4 10 4 12 4*0 4 10
  //   4 12 4*0 4 10 4 12 4*0 4 10 4 12 4*0 4 10 4 12 4*0 4 10 4 12 4*0 4 10 4 12 4*0 4 10 4 12 4*0 4 10 4
  //   12 4*0 4 10 4 12 4*0 4 10 4 10 4 12 0 0 4 10 4 10 4 12 0 0 4 10 4 10 4 12 0 0 4 10 4 10 4 12 0 0 4
  //   10 4 10 4 12 0 0 4 10 4 10 4 12 0 0 4 10 4 10 4 12 0 0 4 10 4 10 4 12 0 0 4 10 4 10 4 12 0 0 4 10 4
  //   10 4 12 0 0 4 10 4 10 4 12 0 0 4 10 4 10 4 12 0 0 4 10 4 10 4 12 0 0 4 10 4 10 4 12 0 0 4 10 4 10 4
  //   12 0 0 4 10 4 10 4 12 0 0 4 10 6*0 4 10 6*0 4 10 6*0 4 10 6*0 4 10 6*0 4 10 6*0 4 10 6*0 4 10 6*0 4
  //   10 6*0 4 10 6*0 4 10 6*0 4 10 6*0 4 10 6*0 4 10 6*0 4 10 6*0 4 10 6*0 4 10 6*0 4 10 6*0 4 10 6*0 4
  //   10 6*0 4 10 6*0 4 10 6*0 4 10 6*0 4 10 6*0 4 10 6*0 4 10 6*0 4 10 6*0 4 10 6*0 4 10 6*0 4 10 6*0 4
  //   10 6*0 4 10 6*0 4 10 6*0 4 10 6*0 4 10 6*0 4 10 6*0 4 10 6*0 4 10 6*0 4 10 6*0 4 10 6*0 4 10 6*0 4
  //   10 6*0 4 10 6*0 4 10 6*0 4 10 6*0 4 10 6*0 4 10 6*0 4 10 6*0 4 10 6*0 4 10 6*0 4 10 6*0 4 10 6*0 4
  //   10 6*0 4 10 6*0 4 10 6*0 4 10 6*0 4 10 6*0 4 10 6*0 4 10 6*0 4 10 6*0 4 10 6*0 4 10 6*0 4 10 6*0 4
  //   10 6*0 4 10 2 5*0 4 10 2 5*0 4 10 2 5*0 4 10 2 5*0 4 10 2 5*0 4 10 2 5*0 4 10 2 5*0 4 10 2 5*0 4 10
  //   2 5*0 4 10 2 5*0 4 10 2 5*0 4 10 2 5*0 4 10 2 5*0 4 10 2 5*0 4 10 2 5*0 4 10 2 5*0 4 10 2 5*0 4 10 2
  //   5*0 4 10 2 5*0 4 10 2 5*0 4 10 2 5*0 4 10 2 5*0 4 10 2 5*0 4 10 2 5*0 4 10 2 5*0 4 10 2 5*0 4 10 2
  //   5*0 4 10 2 5*0 4 10 2 5*0 4 10 2 5*0 4 10 2 5*0 4 10 2 5*0 4 10 2 5*0 4 10 2 5*0 4 10 2 5*0 4 10 2
  //   5*0 4 10 2 5*0 4 10 2 5*0 4 10 2 5*0 4 10 2 5*0 4 10 2 5*0 4 10 2 5*0 4 10 2 5*0 4 10 2 5*0 4 10 2
  //   5*0 4 10 2 5*0 4 10 2 5*0 4 10 2 5*0 4 10 2 5*0 4 10 2 5*0 4 10 2 5*0 4 10 2 5*0 4 10 2 5*0 4 10 2
  //   5*0 4 10 2 5*0 4 10 2 5*0 4 10 2 5*0 4 10 2 5*0 4 10 2 5*0 4 10 2 5*0 4 10 2 5*0 4 10 2 5*0 4 10 2
  //   5*0 4 10 2 5*0 4 10 6*0 4 10 6*0 4 10 6*0 4 10 6*0 4 10 6*0 4 10 6*0 4 10 6*0 4 10 6*0 4 10 6*0 4 10
  //   6*0 4 10 6*0 4 10 6*0 4 10 6*0 4 10 6*0 4 10 6*0 4 10 6*0 4 10 6*0 4 10 6*0 4 10 6*0 4 10 6*0 4 10
  //   6*0 4 10 6*0 4 10 6*0 4 10 6*0 4 10 6*0 4 10 6*0 4 10 6*0 4 10 6*0 4 10 6*0 4 10 6*0 4 10 6*0 4 10
  //   6*0 4 10 6*0 4 10 6*0 4 10 6*0 4 10 6*0 4 10 6*0 4 10 6*0 4 10 6*0 4 10 6*0 4 10 6*0 4 10 6*0 4 10
  //   6*0 4 10 6*0 4 10 6*0 4 10 6*0 4 10 6*0 4 10 6*0 4 10 6*0 4 10 6*0 4 10 6*0 4 10 6*0 4 10 6*0 4 10
  //   6*0 4 10 6*0 4 10 6*0 4 10 6*0 4 10 6*0 4 10 6*0 4 10 6*0 4 10 6*0 4 10 6*0 4 10 6*0 4 10 6*0 4 10
  //   6*0 4 10 6*0 4 10 6*0 4 10 6*0 4 10 6*0 4 10 6*0 4 10 6*0 4 10 6*0 4 10 6*0 4 10 6*0 4 10 6*0 4 10
  //   6*0 4 10 6*0 4 10 6*0 4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
  //   contents of rom_3 (hex, n*v repeats v):
  //   0 0 93 4 6*0 93 4 6*0 93 4 6*0 93 4 6*0 93 4 6*0 93 4 6*0 93 4 6*0 93 4 6*0 93 4 6*0 93 4 6*0 93 4
  //   6*0 93 4 6*0 93 4 6*0 93 4 6*0 93 4 6*0 93 4 6*0 93 4 6*0 93 4 6*0 93 4 6*0 93 4 6*0 93 4 6*0 93 4
  //   6*0 93 4 6*0 93 4 6*0 93 4 6*0 93 4 6*0 93 4 6*0 93 4 6*0 93 4 6*0 93 4 6*0 93 4 6*0 93 4 6*0 93 4
  //   6*0 93 4 6*0 93 4 6*0 93 4 6*0 93 4 6*0 93 4 6*0 93 4 6*0 93 4 6*0 93 4 6*0 93 4 6*0 93 4 6*0 93 4
  //   6*0 93 4 6*0 93 4 6*0 93 4 6*0 93 4 7*0 93 4 6*0 93 4 6*0 93 4 6*0 93 4 6*0 93 4 6*0 93 4 6*0 93 4
  //   6*0 93 4 6*0 93 4 6*0 93 4 6*0 93 4 6*0 93 4 6*0 93 4 6*0 93 4 6*0 93 4 6*0 93 4 6*0 9 4 93 4 4*0 9
  //   4 93 4 4*0 9 4 93 4 4*0 9 4 93 4 4*0 9 4 93 4 4*0 9 4 93 4 4*0 9 4 93 4 4*0 9 4 93 4 4*0 9 4 93 4
  //   4*0 9 4 93 4 4*0 9 4 93 4 4*0 9 4 93 4 4*0 9 4 93 4 4*0 9 4 93 4 4*0 9 4 93 4 4*0 9 4 93 4 0 0 0 63
  //   4 6*0 63 4 6*0 63 4 6*0 63 4 6*0 63 4 6*0 63 4 6*0 63 4 6*0 63 4 6*0 63 4 6*0 63 4 6*0 63 4 6*0 63 4
  //   6*0 63 4 6*0 63 4 6*0 63 4 6*0 63 4 6*0 63 4 6*0 63 4 6*0 63 4 6*0 63 4 6*0 63 4 6*0 63 4 6*0 63 4
  //   6*0 63 4 6*0 63 4 6*0 63 4 6*0 63 4 6*0 63 4 6*0 63 4 6*0 63 4 6*0 63 4 6*0 63 4 6*0 63 4 6*0 63 4
  //   6*0 63 4 6*0 63 4 6*0 63 4 6*0 63 4 6*0 63 4 6*0 63 4 6*0 63 4 6*0 63 4 6*0 63 4 6*0 63 4 6*0 63 4
  //   6*0 63 4 6*0 63 4 6*0 63 4 7*0 63 4 6*0 63 4 6*0 63 4 6*0 63 4 6*0 63 4 6*0 63 4 6*0 63 4 6*0 63 4
  //   6*0 63 4 6*0 63 4 6*0 63 4 6*0 63 4 6*0 63 4 6*0 63 4 6*0 63 4 6*0 63 4 6*0 9 4 63 4 4*0 9 4 63 4
  //   4*0 9 4 63 4 4*0 9 4 63 4 4*0 9 4 63 4 4*0 9 4 63 4 4*0 9 4 63 4 4*0 9 4 63 4 4*0 9 4 63 4 4*0 9 4
  //   63 4 4*0 9 4 63 4 4*0 9 4 63 4 4*0 9 4 63 4 4*0 9 4 63 4 4*0 9 4 63 4 4*0 9 4 63 4 0 0 0 cb 4 6*0 cb
  //   4 6*0 cb 4 6*0 cb 4 6*0 cb 4 6*0 cb 4 6*0 cb 4 6*0 cb 4 6*0 cb 4 6*0 cb 4 6*0 cb 4 6*0 cb 4 6*0 cb 4
  //   6*0 cb 4 6*0 cb 4 6*0 cb 4 6*0 cb 4 6*0 cb 4 6*0 cb 4 6*0 cb 4 6*0 cb 4 6*0 cb 4 6*0 cb 4 6*0 cb 4
  //   6*0 cb 4 6*0 cb 4 6*0 cb 4 6*0 cb 4 6*0 cb 4 6*0 cb 4 6*0 cb 4 6*0 cb 4 6*0 cb 4 6*0 cb 4 6*0 cb 4
  //   6*0 cb 4 6*0 cb 4 6*0 cb 4 6*0 cb 4 6*0 cb 4 6*0 cb 4 6*0 cb 4 6*0 cb 4 6*0 cb 4 6*0 cb 4 6*0 cb 4
  //   6*0 cb 4 6*0 cb 4 6*0 cb 4 6*0 cb 4 6*0 cb 4 6*0 cb 4 6*0 cb 4 6*0 cb 4 6*0 cb 4 6*0 cb 4 6*0 cb 4
  //   6*0 cb 4 6*0 cb 4 6*0 cb 4 6*0 cb 4 6*0 cb 4 6*0 cb 4 6*0 cb 4 6*0 b 4 6*0 b 4 6*0 b 4 6*0 b 4 6*0 b
  //   4 6*0 b 4 6*0 b 4 6*0 b 4 6*0 b 4 6*0 b 4 6*0 b 4 6*0 b 4 6*0 b 4 6*0 b 4 6*0 b 4 6*0 b 4 6*0 b 4
  //   6*0 b 4 6*0 b 4 6*0 b 4 6*0 b 4 6*0 b 4 6*0 b 4 6*0 b 4 6*0 b 4 6*0 b 4 6*0 b 4 6*0 b 4 6*0 b 4 6*0
  //   b 4 6*0 b 4 6*0 b 4 6*0 b 4 6*0 b 4 6*0 b 4 6*0 b 4 6*0 b 4 6*0 b 4 6*0 b 4 6*0 b 4 6*0 b 4 6*0 b 4
  //   6*0 b 4 6*0 b 4 6*0 b 4 6*0 b 4 6*0 b 4 6*0 b 4 6*0 b 4 6*0 b 4 6*0 b 4 6*0 b 4 6*0 b 4 6*0 b 4 6*0
  //   b 4 6*0 b 4 6*0 b 4 6*0 b 4 6*0 b 4 6*0 b 4 6*0 b 4 6*0 b 4 6*0 b 4 6*0 b 4 6*0 fb 4 6*0 fb 4 6*0 fb
  //   4 6*0 fb 4 6*0 fb 4 6*0 fb 4 6*0 fb 4 6*0 fb 4 6*0 fb 4 6*0 fb 4 6*0 fb 4 6*0 fb 4 6*0 fb 4 6*0 fb 4
  //   6*0 fb 4 6*0 fb 4 6*0 fb 4 6*0 fb 4 6*0 fb 4 6*0 fb 4 6*0 fb 4 6*0 fb 4 6*0 fb 4 6*0 fb 4 6*0 fb 4
  //   6*0 fb 4 6*0 fb 4 6*0 fb 4 6*0 fb 4 6*0 fb 4 6*0 fb 4 6*0 fb 4 6*0 fb 4 6*0 fb 4 6*0 fb 4 6*0 fb 4
  //   6*0 fb 4 6*0 fb 4 6*0 fb 4 6*0 fb 4 6*0 fb 4 6*0 fb 4 6*0 fb 4 6*0 fb 4 6*0 fb 4 6*0 fb 4 6*0 fb 4
  //   6*0 fb 4 6*0 fb 4 6*0 fb 4 6*0 fb 4 6*0 fb 4 6*0 fb 4 6*0 fb 4 6*0 fb 4 6*0 fb 4 6*0 fb 4 6*0 fb 4
  //   6*0 fb 4 6*0 fb 4 6*0 fb 4 6*0 fb 4 6*0 fb 4 6*0 fb 4 5767*0 9 4 6*0 9 4 6*0 9 4 6*0 9 4 6*0 9 4 6*0
  //   9 4 6*0 9 4 6*0 9 4 6*0 9 4 6*0 9 4 6*0 9 4 6*0 9 4 6*0 9 4 6*0 9 4 6*0 9 4 6*0 9 4 6*0 9 4 6*0 9 4
  //   6*0 9 4 6*0 9 4 6*0 9 4 6*0 9 4 6*0 9 4 6*0 9 4 6*0 9 4 6*0 9 4 6*0 9 4 6*0 9 4 6*0 9 4 6*0 9 4 6*0
  //   9 4 6*0 9 4 6*0 9 4 6*0 9 4 6*0 9 4 6*0 9 4 6*0 9 4 6*0 9 4 6*0 9 4 6*0 9 4 6*0 9 4 6*0 9 4 6*0 9 4
  //   6*0 9 4 6*0 9 4 6*0 9 4 6*0 9 4 6*0 9 4 6*0 9 4 6*0 9 4 6*0 9 4 6*0 9 4 6*0 9 4 6*0 9 4 6*0 9 4 6*0
  //   9 4 6*0 9 4 6*0 9 4 6*0 9 4 6*0 9 4 6*0 9 4 6*0 9 4 6*0 9 4 6*0 9 4 646*0 9 4 6*0 9 4 6*0 9 4 6*0 9
  //   4 6*0 9 4 6*0 9 4 6*0 9 4 6*0 9 4 6*0 9 4 6*0 9 4 6*0 9 4 6*0 9 4 6*0 9 4 6*0 9 4 6*0 9 4 6*0 9 4
  //   646*0 9 4 6*0 9 4 6*0 9 4 6*0 9 4 6*0 9 4 6*0 9 4 6*0 9 4 6*0 9 4 6*0 9 4 6*0 9 4 6*0 9 4 6*0 9 4
  //   6*0 9 4 6*0 9 4 6*0 9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
  //   contents of rom_4 (hex, n*v repeats v):
  //   0 0 8 1 6*0 8 1 6*0 8 1 6*0 8 1 6*0 8 1 6*0 8 1 6*0 8 1 6*0 8 1 6*0 8 1 6*0 8 1 6*0 8 1 6*0 8 1 6*0
  //   8 1 6*0 8 1 6*0 8 1 6*0 8 1 6*0 20 1 6*0 20 1 6*0 20 1 6*0 20 1 6*0 20 1 6*0 20 1 6*0 20 1 6*0 20 1
  //   6*0 20 1 6*0 20 1 6*0 20 1 6*0 20 1 6*0 20 1 6*0 20 1 6*0 20 1 6*0 20 1 6*0 80 1 6*0 80 1 6*0 80 1
  //   6*0 80 1 6*0 80 1 6*0 80 1 6*0 80 1 6*0 80 1 6*0 80 1 6*0 80 1 6*0 80 1 6*0 80 1 6*0 80 1 6*0 80 1
  //   6*0 80 1 6*0 80 1 8*0 1 7*0 1 7*0 1 7*0 1 7*0 1 7*0 1 7*0 1 7*0 1 7*0 1 7*0 1 7*0 1 7*0 1 7*0 1 7*0
  //   1 7*0 1 7*0 1 9*0 1 7*0 1 7*0 1 7*0 1 7*0 1 7*0 1 7*0 1 7*0 1 7*0 1 7*0 1 7*0 1 7*0 1 7*0 1 7*0 1
  //   7*0 1 7*0 1 0 0 0 8 1 6*0 8 1 6*0 8 1 6*0 8 1 6*0 8 1 6*0 8 1 6*0 8 1 6*0 8 1 6*0 8 1 6*0 8 1 6*0 8
  //   1 6*0 8 1 6*0 8 1 6*0 8 1 6*0 8 1 6*0 8 1 6*0 20 1 6*0 20 1 6*0 20 1 6*0 20 1 6*0 20 1 6*0 20 1 6*0
  //   20 1 6*0 20 1 6*0 20 1 6*0 20 1 6*0 20 1 6*0 20 1 6*0 20 1 6*0 20 1 6*0 20 1 6*0 20 1 6*0 80 1 6*0
  //   80 1 6*0 80 1 6*0 80 1 6*0 80 1 6*0 80 1 6*0 80 1 6*0 80 1 6*0 80 1 6*0 80 1 6*0 80 1 6*0 80 1 6*0
  //   80 1 6*0 80 1 6*0 80 1 6*0 80 1 8*0 1 7*0 1 7*0 1 7*0 1 7*0 1 7*0 1 7*0 1 7*0 1 7*0 1 7*0 1 7*0 1
  //   7*0 1 7*0 1 7*0 1 7*0 1 7*0 1 9*0 1 7*0 1 7*0 1 7*0 1 7*0 1 7*0 1 7*0 1 7*0 1 7*0 1 7*0 1 7*0 1 7*0
  //   1 7*0 1 7*0 1 7*0 1 7*0 1 0 0 0 2 1 6*0 2 1 6*0 2 1 6*0 2 1 6*0 2 1 6*0 2 1 6*0 2 1 6*0 2 1 6*0 2 1
  //   6*0 2 1 6*0 2 1 6*0 2 1 6*0 2 1 6*0 2 1 6*0 2 1 6*0 2 1 6*0 8 4 6*0 8 4 6*0 8 4 6*0 8 4 6*0 8 4 6*0
  //   8 4 6*0 8 4 6*0 8 4 6*0 8 4 6*0 8 4 6*0 8 4 6*0 8 4 6*0 8 4 6*0 8 4 6*0 8 4 6*0 8 4 6*0 20 10 6*0 20
  //   10 6*0 20 10 6*0 20 10 6*0 20 10 6*0 20 10 6*0 20 10 6*0 20 10 6*0 20 10 6*0 20 10 6*0 20 10 6*0 20
  //   10 6*0 20 10 6*0 20 10 6*0 20 10 6*0 20 10 6*0 80 40 6*0 80 40 6*0 80 40 6*0 80 40 6*0 80 40 6*0 80
  //   40 6*0 80 40 6*0 80 40 6*0 80 40 6*0 80 40 6*0 80 40 6*0 80 40 6*0 80 40 6*0 80 40 6*0 80 40 6*0 80
  //   40 6*0 2 1 6*0 2 1 6*0 2 1 6*0 2 1 6*0 2 1 6*0 2 1 6*0 2 1 6*0 2 1 6*0 2 1 6*0 2 1 6*0 2 1 6*0 2 1
  //   6*0 2 1 6*0 2 1 6*0 2 1 6*0 2 1 6*0 8 4 6*0 8 4 6*0 8 4 6*0 8 4 6*0 8 4 6*0 8 4 6*0 8 4 6*0 8 4 6*0
  //   8 4 6*0 8 4 6*0 8 4 6*0 8 4 6*0 8 4 6*0 8 4 6*0 8 4 6*0 8 4 6*0 20 10 6*0 20 10 6*0 20 10 6*0 20 10
  //   6*0 20 10 6*0 20 10 6*0 20 10 6*0 20 10 6*0 20 10 6*0 20 10 6*0 20 10 6*0 20 10 6*0 20 10 6*0 20 10
  //   6*0 20 10 6*0 20 10 6*0 80 40 6*0 80 40 6*0 80 40 6*0 80 40 6*0 80 40 6*0 80 40 6*0 80 40 6*0 80 40
  //   6*0 80 40 6*0 80 40 6*0 80 40 6*0 80 40 6*0 80 40 6*0 80 40 6*0 80 40 6*0 80 40 6*0 2 1 6*0 2 1 6*0
  //   2 1 6*0 2 1 6*0 2 1 6*0 2 1 6*0 2 1 6*0 2 1 6*0 2 1 6*0 2 1 6*0 2 1 6*0 2 1 6*0 2 1 6*0 2 1 6*0 2 1
  //   6*0 2 1 6*0 8 4 6*0 8 4 6*0 8 4 6*0 8 4 6*0 8 4 6*0 8 4 6*0 8 4 6*0 8 4 6*0 8 4 6*0 8 4 6*0 8 4 6*0
  //   8 4 6*0 8 4 6*0 8 4 6*0 8 4 6*0 8 4 6*0 20 10 6*0 20 10 6*0 20 10 6*0 20 10 6*0 20 10 6*0 20 10 6*0
  //   20 10 6*0 20 10 6*0 20 10 6*0 20 10 6*0 20 10 6*0 20 10 6*0 20 10 6*0 20 10 6*0 20 10 6*0 20 10 6*0
  //   80 40 6*0 80 40 6*0 80 40 6*0 80 40 6*0 80 40 6*0 80 40 6*0 80 40 6*0 80 40 6*0 80 40 6*0 80 40 6*0
  //   80 40 6*0 80 40 6*0 80 40 6*0 80 40 6*0 80 40 6*0 80 40 6*0 6 7*0 6 7*0 6 7*0 6 7*0 6 7*0 6 7*0 6
  //   7*0 6 7*0 6 7*0 6 7*0 6 7*0 6 7*0 6 7*0 6 7*0 6 7*0 6 7*0 12 7*0 12 7*0 12 7*0 12 7*0 12 7*0 12 7*0
  //   12 7*0 12 7*0 12 7*0 12 7*0 12 7*0 12 7*0 12 7*0 12 7*0 12 7*0 12 7*0 42 7*0 42 7*0 42 7*0 42 7*0 42
  //   7*0 42 7*0 42 7*0 42 7*0 42 7*0 42 7*0 42 7*0 42 7*0 42 7*0 42 7*0 42 7*0 42 7*0 2 7*0 2 7*0 2 7*0 2
  //   7*0 2 7*0 2 7*0 2 7*0 2 7*0 2 7*0 2 7*0 2 7*0 2 7*0 2 7*0 2 7*0 2 7*0 2 7*0 9 7*0 9 7*0 9 7*0 9 7*0
  //   9 7*0 9 7*0 9 7*0 9 7*0 9 7*0 9 7*0 9 7*0 9 7*0 9 7*0 9 7*0 9 7*0 9 7*0 18 7*0 18 7*0 18 7*0 18 7*0
  //   18 7*0 18 7*0 18 7*0 18 7*0 18 7*0 18 7*0 18 7*0 18 7*0 18 7*0 18 7*0 18 7*0 18 7*0 48 7*0 48 7*0 48
  //   7*0 48 7*0 48 7*0 48 7*0 48 7*0 48 7*0 48 7*0 48 7*0 48 7*0 48 7*0 48 7*0 48 7*0 48 7*0 48 7*0 8 7*0
  //   8 7*0 8 7*0 8 7*0 8 7*0 8 7*0 8 7*0 8 7*0 8 7*0 8 7*0 8 7*0 8 7*0 8 7*0 8 7*0 8 7*0 8 7*0 21 7*0 21
  //   7*0 21 7*0 21 7*0 21 7*0 21 7*0 21 7*0 21 7*0 21 7*0 21 7*0 21 7*0 21 7*0 21 7*0 21 7*0 21 7*0 21
  //   7*0 24 7*0 24 7*0 24 7*0 24 7*0 24 7*0 24 7*0 24 7*0 24 7*0 24 7*0 24 7*0 24 7*0 24 7*0 24 7*0 24
  //   7*0 24 7*0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
  //   And so on.
  //   And another slice.
  //   This is one 8 bit "slice" of the output control signals.
endmodule

module ALU (
  input  [15:0] A,
  input  [15:0] B,
  input  carry_in,
  input  M,
  input  S0,
  input  S1,
  input  S2,
  input  S3,
  input  result_output_enable,
  input  clock,
  input  sim_only_reset,
  input  store_result,
  input  store_flags,
  output unclocked_zero,
  output clocked_zero,
  output unclocked_negative,
  output clocked_negative,
  output unclocked_carryborrow_out,
  output clocked_carryborrow_out,
  output unclocked_A___B,
  output clocked_A___B,
  output [15:0] tristate_clocked_result,
  output [15:0] unclocked_result,
  output [15:0] clocked_result
);

  wire n74ls181_1_a_b, n74ls181_1_carry_out_bar, n74ls181_2_a_b, n74ls181_2_carry_out_bar, n74ls181_3_a_b,
       n74ls181_3_carry_out_bar, n74ls181_4_a_b, n74ls181_4_carry_out_bar, not_2_out, or_1_out,
       safe_clock_enable_1_clock_out, safe_clock_enable_2_clock_out;

  not not_1 (unclocked_carryborrow_out, n74ls181_4_carry_out_bar);
  not not_2 (not_2_out, carry_in);
  and and_1 (unclocked_A___B, n74ls181_1_a_b, n74ls181_2_a_b, n74ls181_3_a_b, n74ls181_4_a_b);
  _74LS181 u_74ls181_1 (
    .B(B[3:0]), .A(A[3:0]), .M(M), .carry_in_bar(not_2_out), .carry_out_bar(n74ls181_1_carry_out_bar),
    .F(unclocked_result[3:0]), .A_B(n74ls181_1_a_b), .S0(S0), .S1(S1), .S2(S2), .S3(S3));  // open: Y, X
  _74LS181 u_74ls181_2 (
    .B(B[7:4]), .A(A[7:4]), .M(M), .carry_in_bar(n74ls181_1_carry_out_bar),
    .carry_out_bar(n74ls181_2_carry_out_bar), .F(unclocked_result[7:4]), .A_B(n74ls181_2_a_b), .S0(S0),
    .S1(S1), .S2(S2), .S3(S3));  // open: Y, X
  _74LS181 u_74ls181_3 (
    .B(B[11:8]), .A(A[11:8]), .M(M), .carry_in_bar(n74ls181_2_carry_out_bar),
    .carry_out_bar(n74ls181_3_carry_out_bar), .F(unclocked_result[11:8]), .A_B(n74ls181_3_a_b), .S0(S0),
    .S1(S1), .S2(S2), .S3(S3));  // open: Y, X
  _74LS181 u_74ls181_4 (
    .B(B[15:12]), .A(A[15:12]), .M(M), .carry_in_bar(n74ls181_3_carry_out_bar),
    .carry_out_bar(n74ls181_4_carry_out_bar), .F({unclocked_negative, unclocked_result[14:12]}),
    .A_B(n74ls181_4_a_b), .S0(S0), .S1(S1), .S2(S2), .S3(S3));  // open: Y, X
  or or_1 (or_1_out, unclocked_result[0], unclocked_result[1], unclocked_result[2], unclocked_result[3], unclocked_result[4], unclocked_result[5], unclocked_result[6], unclocked_result[7], unclocked_result[8], unclocked_result[9], unclocked_result[10], unclocked_result[11], unclocked_result[12], unclocked_result[13], unclocked_result[14], unclocked_negative);
  safe_clock_enable safe_clock_enable_1 (
    .clock_enable(store_result), .clock_in(clock), .clock_out(safe_clock_enable_1_clock_out));
  safe_clock_enable safe_clock_enable_2 (
    .clock_enable(store_flags), .clock_in(clock), .clock_out(safe_clock_enable_2_clock_out));
  not not_3 (unclocked_zero, or_1_out);
  Register #(.width(16)) result (
    .D({unclocked_negative, unclocked_result[14:0]}), .en(1'b1), .Q(clocked_result),
    .clk(safe_clock_enable_1_clock_out), .clr(sim_only_reset));
  assign tristate_clocked_result = result_output_enable ? clocked_result : 16'bz;  // Controlled_Buffer controlled_buffer_1
  Register #(.width(4)) register_1 (
    .D({unclocked_A___B, unclocked_carryborrow_out, unclocked_negative, unclocked_zero}), .en(1'b1),
    .Q({clocked_A___B, clocked_carryborrow_out, clocked_negative, clocked_zero}),
    .clk(safe_clock_enable_2_clock_out), .clr(sim_only_reset));

  assign unclocked_result[15] = unclocked_negative;
endmodule

module Clock (
  input  enable,
  input  Arduino_Crystal,
  input  Arduino_clock,
  output clock
);

  wire Crystal_clock_out, multiplexer_1_out;

  Clock_part Crystal_clock (.out(Crystal_clock_out));
  Multiplexer #(.enable("false")) multiplexer_1 (
    .in0(Arduino_clock), .in1(Crystal_clock_out), .out(multiplexer_1_out), .sel(Arduino_Crystal));
  safe_clock_enable safe_clock_enable_1 (.clock_enable(enable), .clock_in(multiplexer_1_out), .clock_out(clock));
endmodule

module _74LS181 (
  input  S0,
  input  S1,
  input  S2,
  input  S3,
  input  [3:0] B,
  input  [3:0] A,
  input  M,
  input  carry_in_bar,
  output Y,
  output carry_out_bar,
  output X,
  output [3:0] F,
  output A_B
);

  wire and_1_out, and_2_out, and_3_out, and_4_out, and_5_out, and_6_out, and_7_out, and_8_out, and_9_out,
       and_10_out, and_11_out, and_12_out, and_13_out, and_14_out, and_15_out, and_16_out, and_17_out,
       and_18_out, and_19_out, and_20_out, and_21_out, and_22_out, and_23_out, and_24_out, and_25_out,
       and_26_out, and_27_out, and_28_out, nand_1_out, nand_3_out, nor_1_out, nor_2_out, nor_3_out,
       nor_4_out, nor_5_out, nor_6_out, nor_7_out, nor_8_out, nor_10_out, nor_11_out, nor_12_out, not_1_out,
       not_2_out, not_3_out, not_4_out, not_5_out, xor_1_out, xor_2_out, xor_3_out, xor_4_out;

  not not_1 (not_1_out, B[3]);
  not not_2 (not_2_out, B[2]);
  not not_3 (not_3_out, B[1]);
  not not_4 (not_4_out, B[0]);
  not not_5 (not_5_out, M);
  and and_1 (and_1_out, B[3], S3, A[3]);
  and and_2 (and_2_out, A[3], S2, not_1_out);
  and and_3 (and_3_out, not_1_out, S1);
  and and_4 (and_4_out, S0, B[3]);
  and and_5 (and_5_out, B[2], S3, A[2]);
  and and_6 (and_6_out, A[2], S2, not_2_out);
  and and_7 (and_7_out, not_2_out, S1);
  and and_8 (and_8_out, S0, B[2]);
  and and_9 (and_9_out, B[1], S3, A[1]);
  and and_10 (and_10_out, A[1], S2, not_3_out);
  and and_11 (and_11_out, not_3_out, S1);
  and and_12 (and_12_out, S0, B[1]);
  and and_13 (and_13_out, B[0], S3, A[0]);
  and and_14 (and_14_out, A[0], S2, not_4_out);
  and and_15 (and_15_out, not_4_out, S1);
  and and_16 (and_16_out, S0, B[0]);
  nor nor_1 (nor_1_out, and_1_out, and_2_out);
  nor nor_2 (nor_2_out, and_3_out, and_4_out, A[3]);
  nor nor_3 (nor_3_out, and_5_out, and_6_out);
  nor nor_4 (nor_4_out, and_7_out, and_8_out, A[2]);
  nor nor_5 (nor_5_out, and_9_out, and_10_out);
  nor nor_6 (nor_6_out, and_11_out, and_12_out, A[1]);
  nor nor_7 (nor_7_out, and_13_out, and_14_out);
  nor nor_8 (nor_8_out, and_15_out, and_16_out, A[0]);
  xor xor_1 (xor_1_out, nor_1_out, nor_2_out);
  xor xor_2 (xor_2_out, nor_3_out, nor_4_out);
  xor xor_3 (xor_3_out, nor_5_out, nor_6_out);
  xor xor_4 (xor_4_out, nor_7_out, nor_8_out);
  and and_17 (and_17_out, nor_1_out, nor_4_out);
  and and_18 (and_18_out, nor_1_out, nor_3_out, nor_6_out);
  and and_19 (and_19_out, nor_1_out, nor_3_out, nor_5_out, nor_8_out);
  nand nand_1 (nand_1_out, nor_1_out, nor_3_out, nor_5_out, nor_7_out, carry_in_bar);
  nand nand_2 (X, nor_1_out, nor_3_out, nor_5_out, nor_7_out);
  and and_20 (and_20_out, carry_in_bar, nor_7_out, nor_5_out, nor_3_out, not_5_out);
  and and_21 (and_21_out, nor_5_out, nor_3_out, nor_8_out, not_5_out);
  and and_22 (and_22_out, nor_3_out, nor_6_out, not_5_out);
  and and_23 (and_23_out, nor_4_out, not_5_out);
  and and_24 (and_24_out, carry_in_bar, nor_7_out, nor_5_out, not_5_out);
  and and_25 (and_25_out, nor_5_out, nor_8_out, not_5_out);
  and and_26 (and_26_out, nor_6_out, not_5_out);
  and and_27 (and_27_out, carry_in_bar, nor_7_out, not_5_out);
  and and_28 (and_28_out, nor_8_out, not_5_out);
  nand nand_3 (nand_3_out, carry_in_bar, not_5_out);
  nor nor_9 (Y, nor_2_out, and_17_out, and_18_out, and_19_out);
  nor nor_10 (nor_10_out, and_20_out, and_21_out, and_22_out, and_23_out);
  nor nor_11 (nor_11_out, and_24_out, and_25_out, and_26_out);
  nor nor_12 (nor_12_out, and_27_out, and_28_out);
  or or_1 (carry_out_bar, ~Y, ~nand_1_out);  // OR_Gate
  xor xor_5 (F[3], xor_1_out, nor_10_out);
  xor xor_6 (F[2], xor_2_out, nor_11_out);
  xor xor_7 (F[1], xor_3_out, nor_12_out);
  xor xor_8 (F[0], xor_4_out, nand_3_out);
  and and_29 (A_B, F[3], F[2], F[1], F[0]);
endmodule

module safe_clock_enable (
  input  clock_enable,
  input  clock_in,
  output clock_out
);

  wire nor_1_out, nor_2_out, not_1_out, not_2_out;

  not not_1 (not_1_out, clock_enable);
  not not_2 (not_2_out, clock_in);
  nor nor_1 (nor_1_out, not_1_out, nor_2_out);
  nor nor_2 (nor_2_out, nor_1_out, not_2_out);
  and and_1 (clock_out, nor_1_out, clock_in);
endmodule

module register_bus_R (
  input  [15:0] \input ,
  input  input_enable,
  input  output_enable,
  input  clock,
  input  sim_only_reset,
  output [15:0] content,
  output [15:0] buffered_output
);

  wire safe_clock_enable_1_clock_out;

  safe_clock_enable safe_clock_enable_1 (
    .clock_enable(input_enable), .clock_in(clock), .clock_out(safe_clock_enable_1_clock_out));
  Register #(.width(16)) register_1 (
    .D(\input ), .en(1'b1), .Q(content), .clk(safe_clock_enable_1_clock_out), .clr(sim_only_reset));
  assign buffered_output = output_enable ? content : 16'bz;  // Controlled_Buffer controlled_buffer_1
endmodule

module register_bus_L (
  input  [15:0] \input ,
  input  input_enable,
  input  output_enable,
  input  clock,
  input  sim_only_reset,
  output [15:0] content,
  output [15:0] buffered_output
);

  wire safe_clock_enable_1_clock_out;

  safe_clock_enable safe_clock_enable_1 (
    .clock_enable(input_enable), .clock_in(clock), .clock_out(safe_clock_enable_1_clock_out));
  Register #(.width(16)) register_1 (
    .D(\input ), .en(1'b1), .Q(content), .clk(safe_clock_enable_1_clock_out), .clr(sim_only_reset));
  assign buffered_output = output_enable ? content : 16'bz;  // Controlled_Buffer controlled_buffer_1
endmodule

module program_counter (
  input  in,
  input  output_enable,
  input  [15:0] \input ,
  input  count,
  input  clock,
  input  reset,
  output [15:0] tristate_output,
  output [15:0] contents
);

  Counter #(.width(16), .max('hffff)) counter_1 (
    .load(in), .D(\input ), .count(count), .Q(contents), .clk(clock), .clr(reset));  // open: carry
  assign tristate_output = output_enable ? contents : 16'bz;  // Controlled_Buffer controlled_buffer_1
endmodule

module io_device (
  input  [7:0] in_1,
  input  [7:0] in_2,
  input  Prog_data_sel,
  input  Write_to_mem,
  input  Clock,
  output [7:0] out_6
);

  wire and_1_out, and_2_out, nand_1_out, not_1_out;

  nand nand_1 (nand_1_out, in_2[0], in_2[1], in_2[2], in_2[3], in_2[4], in_2[5], in_2[6], in_2[7]);
  not not_1 (not_1_out, nand_1_out);
  and and_1 (and_1_out, not_1_out, Prog_data_sel);
  and and_2 (and_2_out, and_1_out, Write_to_mem);
  Register register_1 (.D(in_1), .en(and_2_out), .Q(out_6), .clk(Clock), .clr(1'b0));
endmodule

module clipboard (
  input  in_1,
  input  in_2,
  output out_3,
  output out_4,
  output out_5,
  output clock_out
);

  wire A_IN, A_OUT, ACC_IN, ACC_OUT, ALU_A_IS_BUS, ALU_C_IN, ALU_CARRYBORROW_FLAG_CLOCKED,
       ALU_CARRYBORROW_FLAG_IMM, ALU_EQUAL_FLAG_CLOCKED, ALU_EQUAL_FLAG_IMM, ALU_M,
       ALU_NEGATIVE_FLAG_CLOCKED, ALU_NEGATIVE_FLAG_IMM, ALU_OUT, ALU_S0, ALU_S1, ALU_S2, ALU_S3,
       ALU_STORE_FLAGS, ALU_STORE_RESULT, ALU_ZERO_FLAG_CLOCKED, ALU_ZERO_FLAG_IMM, B_IN, B_OUT, C_IN, C_OUT,
       CLOCK_HALT, CONTROL_CLOCK, CU_CARRYBORROW_MIRROR, CU_EQUAL_MIRROR, CU_NEGATIVE_MIRROR, CU_STEP_RESET,
       CU_ZERO_MIRROR, IR_IN, MAR_IN, PC_COUNT, PC_IN, PC_OUT, SIM_ONLY_RESET, SP_IN, SP_OUT;
  wire [2:0] CU_MICROCODE_STEP;
  wire [7:0] A, ACC, ADDRESS, ALU_RESULT_CLOCKED, ALU_RESULT_IMM, B, BUS, C, CU_INSTRUCTION_MIRROR, IR, PC,
       SP;

  Button button_1 (.out(SIM_ONLY_RESET));
  LED led_1 (.in(ACC_IN));
  LED led_2 (.in(ACC_OUT));
  LED led_3 (.in(A_IN));
  LED led_4 (.in(A_OUT));
  LED led_5 (.in(B_IN));
  LED led_6 (.in(B_OUT));
  LED led_7 (.in(C_IN));
  LED led_8 (.in(C_OUT));
  LED led_9 (.in(ALU_STORE_RESULT));
  LED led_10 (.in(ALU_STORE_FLAGS));
  LED led_11 (.in(ALU_OUT));
  LED led_12 (.in(ALU_A_IS_BUS));
  LED led_13 (.in(ALU_S0));
  LED led_14 (.in(ALU_S1));
  LED led_15 (.in(ALU_S2));
  LED led_16 (.in(ALU_S3));
  LED led_17 (.in(ALU_M));
  LED led_18 (.in(ALU_C_IN));
  LED led_19 (.in(MAR_IN));
  LED led_20 (.in(out_4));
  LED led_21 (.in(out_5));
  LED led_22 (.in(out_3));
  LED led_23 (.in(SP_IN));
  LED led_24 (.in(SP_OUT));
  LED led_25 (.in(PC_IN));
  LED led_26 (.in(PC_OUT));
  LED led_27 (.in(PC_COUNT));
  LED led_28 (.in(IR_IN));
  LED led_29 (.in(CU_STEP_RESET));
  LED led_30 (.in(CLOCK_HALT));
  LED led_31 (.in(BUS[7]));
  LED led_32 (.in(BUS[6]));
  LED led_33 (.in(PC[7]));
  LED led_34 (.in(PC[6]));
  LED led_35 (.in(IR[6]));
  LED led_36 (.in(IR[7]));
  LED led_37 (.in(SP[7]));
  LED led_38 (.in(SP[6]));
  LED led_39 (.in(ACC[6]));
  LED led_40 (.in(ACC[7]));
  LED led_41 (.in(A[7]));
  LED led_42 (.in(A[6]));
  LED led_43 (.in(B[6]));
  LED led_44 (.in(B[7]));
  LED led_45 (.in(C[7]));
  LED led_46 (.in(C[6]));
  LED led_47 (.in(ADDRESS[6]));
  LED led_48 (.in(ADDRESS[7]));
  LED led_49 (.in(BUS[5]));
  LED led_50 (.in(BUS[3]));
  LED led_51 (.in(BUS[4]));
  LED led_52 (.in(BUS[2]));
  LED led_53 (.in(PC[2]));
  LED led_54 (.in(PC[3]));
  LED led_55 (.in(PC[5]));
  LED led_56 (.in(PC[4]));
  LED led_57 (.in(IR[5]));
  LED led_58 (.in(IR[4]));
  LED led_59 (.in(IR[3]));
  LED led_60 (.in(IR[2]));
  LED led_61 (.in(SP[2]));
  LED led_62 (.in(SP[5]));
  LED led_63 (.in(SP[3]));
  LED led_64 (.in(SP[4]));
  LED led_65 (.in(ACC[3]));
  LED led_66 (.in(ACC[4]));
  LED led_67 (.in(ACC[2]));
  LED led_68 (.in(ACC[5]));
  LED led_69 (.in(A[3]));
  LED led_70 (.in(A[5]));
  LED led_71 (.in(A[2]));
  LED led_72 (.in(A[4]));
  LED led_73 (.in(B[4]));
  LED led_74 (.in(B[5]));
  LED led_75 (.in(B[2]));
  LED led_76 (.in(B[3]));
  LED led_77 (.in(C[3]));
  LED led_78 (.in(C[4]));
  LED led_79 (.in(C[2]));
  LED led_80 (.in(C[5]));
  LED led_81 (.in(ADDRESS[4]));
  LED led_82 (.in(ADDRESS[5]));
  LED led_83 (.in(ADDRESS[3]));
  LED led_84 (.in(ADDRESS[2]));
  // Probe on BUS
  LED led_85 (.in(BUS[0]));
  LED led_86 (.in(BUS[1]));
  // Probe on PC
  LED led_87 (.in(PC[0]));
  LED led_88 (.in(PC[1]));
  // Probe on IR
  LED led_89 (.in(IR[1]));
  LED led_90 (.in(IR[0]));
  // Probe on SP
  LED led_91 (.in(SP[1]));
  LED led_92 (.in(SP[0]));
  // Probe on ACC
  LED led_93 (.in(ACC[1]));
  LED led_94 (.in(ACC[0]));
  // Probe on A
  LED led_95 (.in(A[1]));
  LED led_96 (.in(A[0]));
  // Probe on B
  LED led_97 (.in(B[0]));
  LED led_98 (.in(B[1]));
  // Probe on C
  LED led_99 (.in(C[1]));
  LED led_100 (.in(C[0]));
  // Probe on ADDRESS
  LED led_101 (.in(ADDRESS[1]));
  LED led_102 (.in(ADDRESS[0]));
  // Probe on BUS
  // Probe on BUS
  // Probe on PC
  // Probe on PC
  // Probe on IR
  // Probe on IR
  // Probe on SP
  // Probe on SP
  // Probe on ACC
  // Probe on ACC
  // Probe on A
  // Probe on A
  // Probe on B
  // Probe on B
  // Probe on C
  // Probe on C
  // Probe on ADDRESS
  // Probe on ADDRESS
  LED led_103 (.in(ALU_RESULT_IMM[7]));
  LED led_104 (.in(ALU_RESULT_IMM[6]));
  LED led_105 (.in(ALU_RESULT_CLOCKED[7]));
  LED led_106 (.in(ALU_RESULT_CLOCKED[6]));
  LED led_107 (.in(ALU_ZERO_FLAG_IMM));
  LED led_108 (.in(ALU_NEGATIVE_FLAG_IMM));
  LED led_109 (.in(ALU_CARRYBORROW_FLAG_IMM));
  LED led_110 (.in(ALU_EQUAL_FLAG_IMM));
  LED led_111 (.in(ALU_ZERO_FLAG_CLOCKED));
  LED led_112 (.in(ALU_NEGATIVE_FLAG_CLOCKED));
  LED led_113 (.in(ALU_CARRYBORROW_FLAG_CLOCKED));
  LED led_114 (.in(ALU_EQUAL_FLAG_CLOCKED));
  LED led_115 (.in(CU_INSTRUCTION_MIRROR[7]));
  LED led_116 (.in(CU_MICROCODE_STEP[2]));
  LED led_117 (.in(CU_ZERO_MIRROR));
  LED led_118 (.in(CU_NEGATIVE_MIRROR));
  LED led_119 (.in(CU_CARRYBORROW_MIRROR));
  LED led_120 (.in(CU_EQUAL_MIRROR));
  LED led_121 (.in(clock_out));
  LED led_122 (.in(CONTROL_CLOCK));
  LED led_123 (.in(ALU_RESULT_IMM[3]));
  LED led_124 (.in(ALU_RESULT_IMM[2]));
  LED led_125 (.in(ALU_RESULT_IMM[4]));
  LED led_126 (.in(ALU_RESULT_IMM[5]));
  LED led_127 (.in(ALU_RESULT_CLOCKED[5]));
  LED led_128 (.in(ALU_RESULT_CLOCKED[4]));
  LED led_129 (.in(ALU_RESULT_CLOCKED[3]));
  LED led_130 (.in(ALU_RESULT_CLOCKED[2]));
  LED led_131 (.in(CU_INSTRUCTION_MIRROR[6]));
  LED led_132 (.in(CU_INSTRUCTION_MIRROR[4]));
  LED led_133 (.in(CU_INSTRUCTION_MIRROR[5]));
  LED led_134 (.in(CU_INSTRUCTION_MIRROR[3]));
  LED led_135 (.in(CU_MICROCODE_STEP[0]));
  LED led_136 (.in(CU_MICROCODE_STEP[1]));
  // Probe on ALU_RESULT_IMM
  LED led_137 (.in(ALU_RESULT_IMM[0]));
  LED led_138 (.in(ALU_RESULT_IMM[1]));
  // Probe on ALU_RESULT_CLOCKED
  LED led_139 (.in(ALU_RESULT_CLOCKED[0]));
  LED led_140 (.in(ALU_RESULT_CLOCKED[1]));
  LED led_141 (.in(CU_INSTRUCTION_MIRROR[2]));
  LED led_142 (.in(CU_INSTRUCTION_MIRROR[1]));
  LED led_143 (.in(CU_INSTRUCTION_MIRROR[0]));
  // Probe on ALU_RESULT_IMM
  // Probe on ALU_RESULT_IMM
  // Probe on ALU_RESULT_CLOCKED
  // Probe on ALU_RESULT_CLOCKED
  // Probe on CU_INSTRUCTION_MIRROR
  // Probe on CU_INSTRUCTION_MIRROR
  // Probe on CU_INSTRUCTION_MIRROR
  // Probe on CU_MICROCODE_STEP
  // Probe on CU_MICROCODE_STEP
  // Probe on CU_MICROCODE_STEP

  // Other names for the same wires on the sheet: DATA_CLOCK = clock_out; EXT_CLOCK_PULSE = in_2;
  //   PROG_DATA_MEM = out_3; READ_FROM_MEM = out_5; RESET = in_1; WRITE_TO_MEM = out_4

  // Notes on the sheet:
  //   BIN
  //   BIN
  //   HEX
  //   BIN
  //   HEX
  //   DEC
  //   BIN
  //   HEX
  //   DEC
  //   BIN
  //   HEX
  //   DEC
  //   HEX
  //   DEC
  //   BIN
  //   HEX
  //   DEC
  //   BIN
  //   HEX
  //   DEC
  //   BIN
  //   HEX
  //   DEC
  //   DEC
  //   BIN
  //   HEX
  //   DEC
  //   BIN
  //   HEX
  //   DEC
  //   BIN
  //   HEX
  //   DEC
  //   BIN
  //   HEX
  //   DEC
  //   BIN
  //   HEX
  //   DEC
endmodule

module schem_export (
  input  Halt,
  input  Reset,
  input  Auto_Manual,
  input  Manual_clock,
  output Clock,
  output Control_Clock
);

  wire Auto_clock_out, nand_1_out, nand_2_out, nand_3_out, nand_4_out, nand_5_out, nand_6_out, nand_7_out,
       nand_8_out, nor_1_out, nor_2_out, nor_3_out, nor_4_out, not_1_out, not_2_out;

  Clock_part Auto_clock (.out(Auto_clock_out));
  nand nand_1 (nand_1_out, Auto_Manual, Auto_Manual);
  nor nor_1 (nor_1_out, Halt, Reset);
  nand nand_2 (nand_2_out, Auto_Manual, Manual_clock);
  nand nand_3 (nand_3_out, nand_1_out, Auto_clock_out);
  nand nand_4 (nand_4_out, nor_1_out, nor_1_out);
  nand nand_5 (nand_5_out, nand_2_out, nand_3_out);
  nor nor_2 (nor_2_out, nand_5_out, nand_5_out);
  nor nor_3 (nor_3_out, nand_4_out, nor_4_out);
  nor nor_4 (nor_4_out, nor_3_out, nor_2_out);
  nand nand_6 (nand_6_out, nor_3_out, nand_5_out);
  nand nand_7 (nand_7_out, nand_6_out, nand_6_out);
  nand nand_8 (nand_8_out, nand_7_out, nand_7_out);
  J_K_Flip_Flop j_k_ff_1 (
    .J(1'b1), .clk(nand_7_out), .K(1'b1), .Q(Clock), .preset(1'b0), .en(1'b1), .reset(not_1_out));  // open: Qn
  not not_1 (not_1_out, nor_1_out);
  J_K_Flip_Flop j_k_ff_2 (
    .J(1'b1), .clk(nand_8_out), .K(1'b1), .Q(Control_Clock), .preset(1'b0), .en(1'b1), .reset(not_2_out));  // open: Qn
  not not_2 (not_2_out, nor_1_out);

  // Notes on the sheet:
  //   Safe clock enable
endmodule

module ALU_comparison_test (
  input  [7:0] in_1,
  input  [7:0] in_2,
  input  in_3,
  input  in_4,
  input  in_5,
  input  in_6,
  input  in_7,
  input  in_8,
  output out_9,
  output out_10,
  output [7:0] out_11
);

  wire n74ls181_1_a_b, n74ls181_1_carry_out_bar, n74ls181_2_a_b, n74ls181_2_carry_out_bar, not_2_out;

  not not_1 (out_10, n74ls181_2_carry_out_bar);
  not not_2 (not_2_out, in_3);
  and and_1 (out_9, n74ls181_1_a_b, n74ls181_2_a_b);
  _74LS181 u_74ls181_1 (
    .B(in_2[3:0]), .A(in_1[3:0]), .M(in_4), .carry_in_bar(not_2_out),
    .carry_out_bar(n74ls181_1_carry_out_bar), .F(out_11[3:0]), .A_B(n74ls181_1_a_b), .S0(in_5), .S1(in_6),
    .S2(in_7), .S3(in_8));  // open: Y, X
  _74LS181 u_74ls181_2 (
    .B(in_2[7:4]), .A(in_1[7:4]), .M(in_4), .carry_in_bar(n74ls181_1_carry_out_bar),
    .carry_out_bar(n74ls181_2_carry_out_bar), .F(out_11[7:4]), .A_B(n74ls181_2_a_b), .S0(in_5), .S1(in_6),
    .S2(in_7), .S3(in_8));  // open: Y, X
  // Probe on in_2[3:0]
  // Probe on in_1[3:0]
endmodule

module new_clock_test (
  input  clock_enable,
  input  R,
  input  clock_in,
  input  S,
  input  in_5,
  input  clock_enable_2,
  input  in_7,
  input  clock_in_2,
  input  in_9,
  input  in_10,
  input  in_11,
  input  in_12,
  input  in_13,
  input  in_14,
  output clock_out,
  output out_16,
  output out_17
);

  wire and_1_out, and_2_out, nor_1_out, nor_2_out, nor_3_out, nor_4_out, nor_5_out, nor_6_out, not_1_out,
       not_2_out;

  nor nor_1 (nor_1_out, R, nor_2_out);
  nor nor_2 (nor_2_out, nor_1_out, S);
  safe_clock_enable safe_clock_enable_1 (.clock_enable(in_5), .clock_in(in_7), .clock_out(out_16));
  safe_clock_enable_disable safe_clock_enable_disable_1 (.clock_enable(in_13), .clock_in(in_14), .clock_out(out_17));
  not not_1 (not_1_out, clock_enable);
  not not_2 (not_2_out, clock_in);
  nor nor_3 (nor_3_out, not_1_out, nor_4_out);
  nor nor_4 (nor_4_out, nor_3_out, not_2_out);
  and and_1 (and_1_out, nor_3_out, clock_in);
  J_K_Flip_Flop j_k_ff_1 (
    .J(clock_enable_2), .clk(clock_in_2), .K(in_9), .preset(in_10), .en(in_11), .reset(in_12));  // open: Q, Qn
  and and_2 (and_2_out, not_1_out, not_2_out);
  nor nor_5 (nor_5_out, and_2_out, nor_6_out);
  nor nor_6 (nor_6_out, nor_5_out, and_1_out);
  and and_3 (clock_out, nor_5_out, clock_in);

  // Notes on the sheet:
  //   Q
  //   Q'
  //   Reset
  //   Set
endmodule

module safe_clock_enable_disable (
  input  clock_enable,
  input  clock_in,
  output clock_out
);

  wire and_1_out, and_2_out, nor_1_out, nor_2_out, nor_3_out, nor_4_out, not_1_out, not_2_out;

  not not_1 (not_1_out, clock_enable);
  nor nor_1 (nor_1_out, not_1_out, nor_2_out);
  nor nor_2 (nor_2_out, nor_1_out, not_2_out);
  not not_2 (not_2_out, clock_in);
  and and_1 (and_1_out, nor_1_out, clock_in);
  and and_2 (and_2_out, not_1_out, not_2_out);
  nor nor_3 (nor_3_out, and_2_out, nor_4_out);
  nor nor_4 (nor_4_out, nor_3_out, and_1_out);
  and and_3 (clock_out, nor_3_out, clock_in);

  // Notes on the sheet:
  //   Reset
  //   Set
endmodule
